// Logisim project Circuitos_Obligatorio.circ as structural Verilog: 6 circuits, main circuit main
module main (
);

  wire abajo, and_1_out, and_2_out, and_3_out, and_4_out, and_5_out, and_10_out, and_11_out, arriba, b0, b1,
       b2, b3, b4, b5, b6, b7, b8, b9, button_1_out, button_2_out, button_4_out, button_5_out, clock_1_out,
       clock_2_out, comparator_1_eq, comparator_2_eq, comparator_3_eq, comparator_4_eq, comparator_5_eq,
       comparator_6_eq, comparator_8_eq, comparator_11_gt, comparator_12_eq, contador_1_bit0,
       contador_1_bit9, contador_1_out_4, contador_1_out_5, contador_1_out_6, contador_1_out_7,
       contador_1_out_8, contador_1_out_9, contador_1_out_10, contador_1_out_11, d_ff_1_q, Derecha, et1, et2,
       et3, et4, et5, et6, et7, et8, et9, et10, et11, et12, et13, et14, et15, et16, Izquierda, me_1_puertaa,
       me_1_puertab, nand_1_out, nand_2_out, nand_3_out, nand_4_out, not_4_out, not_5_out, not_6_out,
       not_7_out, not_8_out, not_9_out, not_10_out, not_13_out, not_14_out, or_1_out, or_2_out, or_3_out,
       or_4_out, or_5_out, or_9_out, or_12_out, Pd, Pi, por_1_out, por_2_out, register_1_q, register_2_q,
       Rst, shift_register_1_p1, shift_register_1_p2, shift_register_2_p10, shift_register_3_p10, xor_1_out,
       xor_2_out, xor_3_out, xor_4_out;
  wire [1:0] not_11_out;
  wire [2:0] counter_1_q, movy_1_posexit;
  wire [3:0] contador_1_salcent, contador_1_saldec, contador_1_saluni, contadorrecord_1_cout,
       contadorrecord_1_dout, contadorrecord_1_uout, movx_1_posexit, movx_2_posexit;
  wire [15:0] and_6_out, and_7_out, and_8_out, decoder_1_out15, decoder_2_out15, multiplexer_1_out,
       multiplexer_2_out, multiplexer_3_out, multiplexer_4_out, multiplexer_5_out, multiplexer_6_out,
       multiplexer_7_out, multiplexer_8_out, multiplexer_9_out, multiplexer_10_out, multiplexer_11_out,
       multiplexer_12_out, or_6_out, or_7_out, or_8_out, or_10_out, or_11_out, shift_register_1_p14,
       shift_register_3_p33;

  POR por_1 (.out(por_1_out));
  xor xor_1 (xor_1_out, d_ff_1_q, abajo);
  xor xor_2 (xor_2_out, d_ff_1_q, Derecha);
  or or_1 (or_1_out, Rst, por_1_out);
  or or_2 (or_2_out, or_1_out, xor_2_out);
  xor xor_3 (xor_3_out, d_ff_1_q, arriba);
  xor xor_4 (xor_4_out, d_ff_1_q, Izquierda);
  or or_3 (or_3_out, xor_1_out, or_1_out);
  movX movx_1 (.left(xor_4_out), .right(or_2_out), .reset(or_1_out), .posExit(movx_1_posexit));
  movY movy_1 (.down(or_3_out), .up(xor_3_out), .reset(or_1_out), .posExit(movy_1_posexit));
  Decoder #(.select(4)) decoder_1 (
    .out0(decoder_1_out15[15]), .out1(decoder_1_out15[14]), .out2(decoder_1_out15[13]),
    .out3(decoder_1_out15[12]), .out4(decoder_1_out15[11]), .out5(decoder_1_out15[10]),
    .out6(decoder_1_out15[9]), .out7(decoder_1_out15[8]), .out8(decoder_1_out15[7]),
    .out9(decoder_1_out15[6]), .out10(decoder_1_out15[5]), .out11(decoder_1_out15[4]),
    .out12(decoder_1_out15[3]), .out13(decoder_1_out15[2]), .out14(decoder_1_out15[1]),
    .out15(decoder_1_out15[0]), .sel(movx_1_posexit));  // open: en
  Clock clock_1 (.out(clock_1_out));
  and and_1 (and_1_out, not_13_out, clock_1_out);
  POR #(.porsize(1)) por_2 (.out(por_2_out));
  // Shift_Register #(.length(16)) shift_register_1: pin names not known; wires that end beside it: shift_register_1_p1, shift_register_1_p2, and_1_out, shift_register_1_p14[15], 1'b1, 1'b0, 1'b0, 1'b0, 1'b1, 1'b1, 1'b0, 1'b1, por_2_out, shift_register_1_p14[0], shift_register_1_p14[1], shift_register_1_p14[2], shift_register_1_p14[3], shift_register_1_p14[4], shift_register_1_p14[5], shift_register_1_p14[6], shift_register_1_p14[7]
  not not_1 (shift_register_1_p2, por_2_out);
  // Shift_Register #(.length(16)) shift_register_2: pin names not known; wires that end beside it: 1'b0, 1'b1, 1'b0, 1'b0, 1'b0, 1'b1, 1'b0, 1'b1, por_2_out, shift_register_2_p10, and_1_out, et16, 1'b0, 1'b1, 1'b0, 1'b1, 1'b1, 1'b1, 1'b0, 1'b0, shift_register_1_p14[15], shift_register_1_p14[8], shift_register_1_p14[9], shift_register_1_p14[10], shift_register_1_p14[11], shift_register_1_p14[12], shift_register_1_p14[13], shift_register_1_p14[14], et1, et2, et3, et4, et5, et6, et7, et8
  not not_2 (shift_register_2_p10, por_2_out);
  // Shift_Register #(.length(16)) shift_register_3: pin names not known; wires that end beside it: 1'b0, 1'b0, 1'b0, 1'b1, 1'b0, 1'b1, 1'b0, 1'b0, por_2_out, shift_register_3_p10, and_1_out, shift_register_3_p33[15], 1'b0, 1'b1, 1'b0, 1'b1, 1'b0, 1'b0, 1'b0, 1'b1, 1'b1, 1'b0, 1'b0, 1'b0, et16, et9, et10, et11, et12, et13, et14, et15, shift_register_3_p33[0], shift_register_3_p33[1], shift_register_3_p33[2], shift_register_3_p33[3], shift_register_3_p33[4], shift_register_3_p33[5], shift_register_3_p33[6], shift_register_3_p33[7], shift_register_3_p33[8], shift_register_3_p33[9], shift_register_3_p33[10], shift_register_3_p33[11]
  not not_3 (shift_register_3_p10, por_2_out);
  or or_4 (or_4_out, arriba, Derecha, Izquierda, abajo);
  Comparator #(.mode("unsigned"), .width(3)) comparator_1 (
    .a(movy_1_posexit), .b(3'b111), .eq(comparator_1_eq));  // open: gt, lt
  Comparator #(.mode("unsigned"), .width(3)) comparator_2 (
    .a(movy_1_posexit), .b(3'b110), .eq(comparator_2_eq));  // open: gt, lt
  Comparator #(.mode("unsigned"), .width(3)) comparator_3 (
    .a(movy_1_posexit), .b(3'b101), .eq(comparator_3_eq));  // open: gt, lt
  Comparator #(.mode("unsigned"), .width(3)) comparator_4 (
    .a(movy_1_posexit), .b(3'b100), .eq(comparator_4_eq));  // open: gt, lt
  Comparator #(.mode("unsigned"), .width(3)) comparator_5 (
    .a(movy_1_posexit), .b(3'b011), .eq(comparator_5_eq));  // open: gt, lt
  Comparator #(.mode("unsigned"), .width(3)) comparator_6 (
    .a(movy_1_posexit), .b(3'b010), .eq(comparator_6_eq));  // open: gt, lt
  Comparator #(.mode("unsigned"), .width(3)) comparator_7 (
    .a(movy_1_posexit), .b(3'b001), .eq(shift_register_1_p1));  // open: gt, lt
  Comparator #(.mode("unsigned"), .width(3)) comparator_8 (
    .a(movy_1_posexit), .b(3'b000), .eq(comparator_8_eq));  // open: gt, lt
  Register #(.width(1)) register_1 (.D(and_3_out), .en(or_9_out), .clk(or_4_out), .Q(register_1_q), .clr(or_5_out));
  or or_5 (or_5_out, Rst, comparator_8_eq);
  not not_4 (not_4_out, Rst);
  Multiplexer #(.width(16)) multiplexer_1 (
    .in0({16{1'b0}}), .in1(decoder_1_out15), .out(multiplexer_1_out), .sel(comparator_1_eq));
  Multiplexer #(.width(16)) multiplexer_2 (
    .in0({16{1'b0}}), .in1(decoder_1_out15), .out(multiplexer_2_out), .sel(comparator_2_eq));
  Multiplexer #(.width(16)) multiplexer_3 (
    .in0({16{1'b0}}), .in1(decoder_1_out15), .out(multiplexer_3_out), .sel(comparator_3_eq));
  Multiplexer #(.width(16)) multiplexer_4 (
    .in0({16{1'b0}}), .in1(decoder_1_out15), .out(multiplexer_4_out), .sel(comparator_4_eq));
  Multiplexer #(.width(16)) multiplexer_5 (
    .in0({16{1'b0}}), .in1(decoder_1_out15), .out(multiplexer_5_out), .sel(comparator_5_eq));
  Multiplexer #(.width(16)) multiplexer_6 (
    .in0({16{1'b0}}), .in1(decoder_1_out15), .out(multiplexer_6_out), .sel(comparator_6_eq));
  Multiplexer #(.width(16)) multiplexer_7 (
    .in0({16{1'b0}}), .in1(decoder_1_out15), .out(multiplexer_7_out), .sel(shift_register_1_p1));
  Multiplexer #(.width(16)) multiplexer_8 (
    .in0({16{1'b0}}), .in1(decoder_1_out15), .out(multiplexer_8_out), .sel(comparator_8_eq));
  Multiplexer #(.width(16)) multiplexer_9 (
    .in0(shift_register_1_p14), .in1({16{1'b0}}), .out(multiplexer_9_out), .sel(register_2_q));
  not not_5 (not_5_out, register_1_q);
  not not_6 (not_6_out, Rst);
  and and_2 (and_2_out, register_1_q, not_4_out, comparator_8_eq);
  Multiplexer #(.width(16)) multiplexer_10 (
    .in0({et1, et2, et3, et4, et5, et6, et7, et8, et9, et10, et11, et12, et13, et14, et15, et16}),
    .in1({16{1'b0}}), .out(multiplexer_10_out), .sel(register_2_q));
  and and_3 (and_3_out, comparator_1_eq, not_5_out, not_6_out);
  assign or_6_out = multiplexer_2_out | multiplexer_9_out;  // OR_Gate or_6, 16 bits wide
  assign or_7_out = multiplexer_5_out | multiplexer_10_out;  // OR_Gate or_7, 16 bits wide
  assign or_8_out = multiplexer_7_out | multiplexer_11_out;  // OR_Gate or_8, 16 bits wide
  Multiplexer #(.width(16)) multiplexer_11 (
    .in0(shift_register_3_p33), .in1({16{1'b0}}), .out(multiplexer_11_out), .sel(register_2_q));
  or or_9 (or_9_out, and_3_out, and_2_out);
  not not_7 (not_7_out, Pi);
  not not_8 (not_8_out, Pd);
  contador contador_1 (
    .clock(or_9_out), .reset(comparator_12_eq), .bit9(contador_1_bit9), .out_4(contador_1_out_4),
    .out_5(contador_1_out_5), .out_6(contador_1_out_6), .out_7(contador_1_out_7), .out_8(contador_1_out_8),
    .out_9(contador_1_out_9), .out_10(contador_1_out_10), .out_11(contador_1_out_11), .bit0(contador_1_bit0),
    .salDec(contador_1_saldec), .salCent(contador_1_salcent), .salUni(contador_1_saluni));
  nand nand_1 (nand_1_out, decoder_2_out15[11], not_7_out);
  nand nand_2 (nand_2_out, not_8_out, decoder_2_out15[6]);
  nand nand_3 (nand_3_out, decoder_2_out15[9], not_9_out);
  not not_9 (not_9_out, Pi);
  not not_10 (not_10_out, Pd);
  nand nand_4 (nand_4_out, not_10_out, decoder_2_out15[4]);
  Multiplexer #(.select(2), .width(16)) multiplexer_12 (
    .in1(16'h20), .in2(16'h400), .in3(16'h420), .out(multiplexer_12_out), .sel(not_11_out));  // open: in0
  and and_4 (and_4_out, button_5_out, nand_1_out, nand_2_out);
  and and_5 (and_5_out, button_2_out, nand_3_out, nand_4_out);
  DotMatrix #(.inputtype("row"), .matrixcols(16), .matrixrows(8)) dotmatrix_1 (
    .row0(multiplexer_1_out), .row1(or_6_out), .row2(multiplexer_3_out), .row3(multiplexer_4_out),
    .row4(or_7_out), .row5(multiplexer_6_out), .row6(or_8_out), .row7(multiplexer_8_out));
  Comparator #(.width(16)) comparator_9 (.a(multiplexer_12_out), .b(16'h400), .eq(Pd));  // open: gt, lt
  Comparator #(.width(16)) comparator_10 (.a(multiplexer_12_out), .b(16'h20), .eq(Pi));  // open: gt, lt
  assign or_10_out = multiplexer_12_out | decoder_2_out15;  // OR_Gate or_10, 16 bits wide
  LED led_1 (.in(contador_1_bit9));
  LED led_2 (.in(contador_1_out_4));
  LED led_3 (.in(contador_1_out_5));
  LED led_4 (.in(contador_1_out_6));
  Hex_Digit_Display hex_digit_display_1 (.value(contador_1_salcent));  // open: dp
  Button button_1 (.out(button_1_out));
  DotMatrix #(.inputtype("row"), .matrixcols(16), .matrixrows(8)) dotmatrix_2 (
    .row0(16'h420), .row1(16'h420), .row2(16'h420), .row3(16'h420), .row4(multiplexer_12_out),
    .row5(multiplexer_12_out), .row6(multiplexer_12_out), .row7(or_10_out));
  Button button_2 (.out(button_2_out));
  LED led_5 (.in(contador_1_out_7));
  LED led_6 (.in(contador_1_out_8));
  LED led_7 (.in(contador_1_out_9));
  LED led_8 (.in(contador_1_out_10));
  Hex_Digit_Display hex_digit_display_2 (.value(contador_1_saldec));  // open: dp
  Button button_3 (.out(Izquierda));
  LED Colision (.in(comparator_11_gt));
  Button button_4 (.out(button_4_out));
  Button button_5 (.out(button_5_out));
  movX movx_2 (.left(and_5_out), .right(and_4_out), .reset(Rst), .posExit(movx_2_posexit));
  LED led_9 (.in(contador_1_out_11));
  LED led_10 (.in(contador_1_bit0));
  Hex_Digit_Display hex_digit_display_3 (.value(contador_1_saluni));  // open: dp
  Button button_6 (.out(arriba));
  Button button_7 (.out(Derecha));
  Button button_8 (.out(abajo));
  LED led_11 (.in(b9));
  LED led_12 (.in(b8));
  LED led_13 (.in(b7));
  Hex_Digit_Display hex_digit_display_4 (.value(contadorrecord_1_cout));  // open: dp
  Decoder #(.select(4)) decoder_2 (
    .out0(decoder_2_out15[15]), .out1(decoder_2_out15[14]), .out2(decoder_2_out15[13]),
    .out3(decoder_2_out15[12]), .out4(decoder_2_out15[11]), .out5(decoder_2_out15[10]),
    .out6(decoder_2_out15[9]), .out7(decoder_2_out15[8]), .out8(decoder_2_out15[7]),
    .out9(decoder_2_out15[6]), .out10(decoder_2_out15[5]), .out11(decoder_2_out15[4]),
    .out12(decoder_2_out15[3]), .out13(decoder_2_out15[2]), .out14(decoder_2_out15[1]),
    .out15(decoder_2_out15[0]), .sel(movx_2_posexit));  // open: en
  LED led_14 (.in(b6));
  LED led_15 (.in(b5));
  LED led_16 (.in(b4));
  LED led_17 (.in(b3));
  Hex_Digit_Display hex_digit_display_5 (.value(contadorrecord_1_dout));  // open: dp
  assign and_6_out = multiplexer_2_out & multiplexer_9_out;  // AND_Gate and_6, 16 bits wide
  assign and_7_out = multiplexer_10_out & multiplexer_5_out;  // AND_Gate and_7, 16 bits wide
  assign and_8_out = multiplexer_11_out & multiplexer_7_out;  // AND_Gate and_8, 16 bits wide
  LED led_18 (.in(b2));
  LED led_19 (.in(b1));
  LED led_20 (.in(b0));
  Hex_Digit_Display hex_digit_display_6 (.value(contadorrecord_1_uout));  // open: dp
  ME me_1 (.A(button_1_out), .B(button_4_out), .PuertaA(me_1_puertaa), .PuertaB(me_1_puertab));
  assign or_11_out = and_6_out | and_7_out | and_8_out;  // OR_Gate or_11, 16 bits wide
  not not_11 (not_11_out[0], me_1_puertab);
  not not_12 (not_11_out[1], me_1_puertaa);
  Comparator #(.mode("unsigned"), .width(16)) comparator_11 (
    .a(or_11_out), .b({16{1'b0}}), .gt(comparator_11_gt));  // open: eq, lt
  or or_12 (or_12_out, comparator_11_gt, d_ff_1_q);
  Clock clock_2 (.out(clock_2_out));
  not not_13 (not_13_out, d_ff_1_q);
  contadorRecord contadorrecord_1 (
    .ENC(1'b1), .Unidades(contador_1_saluni), .Decenas(contador_1_saldec), .Centenas(contador_1_salcent),
    .bit0(b0), .out_6(b1), .out_7(b2), .out_8(b3), .COut(contadorrecord_1_cout),
    .DOut(contadorrecord_1_dout), .Uout(contadorrecord_1_uout), .out_12(b4), .out_13(b5), .out_14(b6),
    .out_15(b7), .out_16(b8), .bit9(b9));
  D_Flip_Flop d_ff_1 (.D(or_12_out), .clk(clock_2_out), .Q(d_ff_1_q), .reset(comparator_12_eq));  // open: Qn, preset
  and and_9 (Rst, comparator_12_eq, d_ff_1_q);
  not not_14 (not_14_out, register_2_q);
  Register #(.width(1)) register_2 (.D(and_10_out), .clk(clock_2_out), .Q(register_2_q));  // open: en, clr
  and and_10 (and_10_out, not_14_out, d_ff_1_q);
  and and_11 (and_11_out, register_2_q, clock_2_out);
  Counter #(.max('h7), .width(3)) counter_1 (
    .clr(comparator_12_eq), .clk(and_11_out), .Q(counter_1_q));  // open: load, up, count, D, carry
  Comparator #(.width(3)) comparator_12 (.a(3'b110), .b(counter_1_q), .eq(comparator_12_eq));  // open: gt, lt

  // Notes on the sheet:
  //   senial del reseteo
  //   Salida de posicionY
  //   ac
  //   ac
  //   cc
  //   Posx
  //   CROSSY ROAD
  //   ESCOTILLAS DEL ESPACIO
  //   Puerta A
  //   <
  //   Puntaje actual
  //   ^
  //   <
  //   v
  //   Puerta B
  //   >
  //   >
  //   Puntaje record
  //   Registro de Perder
  //   Cuenta 6 ticks dsp de perder, luego reinicio.
endmodule

module movX (
  input  left,
  input  right,
  input  reset,
  output [3:0] posExit
);

  wire comparator_1_gt, comparator_2_lt, nor_1_out;
  wire [1:0] and_2_out;
  wire [3:0] adder_1_out, multiplexer_1_out, multiplexer_2_out, subtractor_1_out;

  Register #(.width(4)) register_1 (.D(multiplexer_2_out), .clk(nor_1_out), .Q(posExit));  // open: en, clr
  nor nor_1 (nor_1_out, left, right);
  Comparator #(.mode("unsigned"), .width(4)) comparator_1 (
    .a(posExit), .b(4'b0000), .gt(comparator_1_gt));  // open: eq, lt
  Comparator #(.mode("unsigned"), .width(4)) comparator_2 (
    .a(posExit), .b(4'b1111), .lt(comparator_2_lt));  // open: gt, eq
  Adder #(.width(4)) adder_1 (.a(posExit), .b(4'b0001), .out(adder_1_out));  // open: cin, cout
  Subtractor #(.width(4)) subtractor_1 (.a(posExit), .b(4'b0001), .out(subtractor_1_out));  // open: bin, bout
  and and_1 (and_2_out[1], left, comparator_1_gt);
  and and_2 (and_2_out[0], right, comparator_2_lt);
  Multiplexer #(.select(2), .width(4)) multiplexer_1 (
    .in0(posExit), .in1(adder_1_out), .in2(subtractor_1_out), .in3(posExit), .out(multiplexer_1_out),
    .sel(and_2_out));
  Multiplexer #(.width(4)) multiplexer_2 (.in0(multiplexer_1_out), .in1(4'b0111), .out(multiplexer_2_out), .sel(reset));

  // Notes on the sheet:
  //   x+1 (der)
  //    (01 der)
  //   x-1 (izq)
  //   codificador
  //   aca decide si puede moverse o no
  //   (10 izq)
endmodule

module movY (
  input  down,
  input  up,
  input  reset,
  output [2:0] posExit
);

  wire comparator_1_gt, comparator_2_lt, nor_1_out;
  wire [1:0] and_2_out;
  wire [2:0] adder_1_out, multiplexer_1_out, multiplexer_2_out, subtractor_1_out;

  nor nor_1 (nor_1_out, down, up);
  Register #(.width(3)) register_1 (.D(multiplexer_2_out), .clk(nor_1_out), .Q(posExit));  // open: en, clr
  Comparator #(.mode("unsigned"), .width(3)) comparator_1 (
    .a(posExit), .b(3'b000), .gt(comparator_1_gt));  // open: eq, lt
  Comparator #(.mode("unsigned"), .width(3)) comparator_2 (
    .a(posExit), .b(3'b111), .lt(comparator_2_lt));  // open: gt, eq
  Adder #(.width(3)) adder_1 (.a(posExit), .b(3'b001), .out(adder_1_out));  // open: cin, cout
  Subtractor #(.width(3)) subtractor_1 (.a(posExit), .b(3'b001), .out(subtractor_1_out));  // open: bin, bout
  and and_1 (and_2_out[1], down, comparator_1_gt);
  and and_2 (and_2_out[0], up, comparator_2_lt);
  Multiplexer #(.select(2), .width(3)) multiplexer_1 (
    .in0(posExit), .in1(adder_1_out), .in2(subtractor_1_out), .in3(posExit), .out(multiplexer_1_out),
    .sel(and_2_out));
  Multiplexer #(.width(3)) multiplexer_2 (.in0(multiplexer_1_out), .in1(3'b000), .out(multiplexer_2_out), .sel(reset));

  // Notes on the sheet:
  //   x+1 (arriba)
  //    (01 ar)
  //   x-1 (abajo)
  //   codificador
  //   aca decide si puede moverse o no
  //   (10 ab)
endmodule

module contador (
  input  clock,
  input  reset,
  output bit9,
  output out_4,
  output out_5,
  output out_6,
  output out_7,
  output out_8,
  output out_9,
  output out_10,
  output out_11,
  output bit0,
  output [3:0] salDec,
  output [3:0] salCent,
  output [3:0] salUni
);

  wire and_1_out, comparator_1_eq, comparator_2_eq, comparator_3_eq, comparator_4_eq, comparator_5_gt,
       multiplexer_3_p5, or_1_out;
  wire [3:0] multiplexer_1_out, multiplexer_2_out, multiplexer_3_p4, multiplier_1_out, register_5_q;
  wire [9:0] adder_1_out, ram_1_dout;

  Register #(.width(4)) register_1 (
    .D(multiplexer_1_out), .clk(comparator_2_eq), .Q(salCent), .clr(reset));  // open: en
  Multiplexer #(.select(4), .width(4)) multiplexer_1 (
    .in0(4'b0001), .in1(4'b0010), .in2(4'b0011), .in3(4'b0100), .in4(4'b0101), .in5(4'b0110), .in6(4'b0111),
    .in7(4'b1000), .in8(4'b1001), .in9(4'b0000), .out(multiplexer_1_out), .sel(salCent));  // open: in10, in11, in12, in13, in14, in15
  Comparator #(.mode("unsigned"), .width(10)) comparator_1 (
    .a({bit9, out_4, out_5, out_6, out_7, out_8, out_9, out_10, out_11, bit0}), .b(10'h3e8),
    .eq(comparator_1_eq));  // open: gt, lt
  Adder #(.width(10)) adder_1 (
    .a({bit9, out_4, out_5, out_6, out_7, out_8, out_9, out_10, out_11, bit0}), .b(10'h5), .out(adder_1_out));  // open: cin, cout
  Register #(.width(4)) register_2 (.D(multiplexer_2_out), .clk(and_1_out), .Q(salDec), .clr(reset));  // open: en
  Register #(.width(10)) register_3 (
    .D(adder_1_out), .clk(clock), .Q({bit9, out_4, out_5, out_6, out_7, out_8, out_9, out_10, out_11, bit0}),
    .clr(or_1_out));  // open: en
  or or_1 (or_1_out, comparator_1_eq, reset);
  Multiplier #(.width(4)) multiplier_1 (.a(multiplexer_2_out), .b(4'b0001), .out(multiplier_1_out));  // open: cin, cout
  Multiplexer #(.select(4), .width(4)) multiplexer_2 (
    .in0(4'b0001), .in1(4'b0010), .in2(4'b0011), .in3(4'b0100), .in4(4'b0101), .in5(4'b0110), .in6(4'b0111),
    .in7(4'b1000), .in8(4'b1001), .in9(4'b0000), .out(multiplexer_2_out), .sel(salDec));  // open: in10, in11, in12, in13, in14, in15
  Comparator #(.width(4)) comparator_2 (.a(multiplier_1_out), .b(4'b0000), .eq(comparator_2_eq));  // open: gt, lt
  Register #(.width(4)) register_4 (.D(multiplexer_3_p4), .clk(clock), .Q(salUni), .clr(reset));  // open: en
  RAM #(.addrWidth(2), .dataWidth(10)) ram_1 (
    .addr(2'b01), .we(comparator_5_gt), .clk(comparator_5_gt),
    .din({bit9, out_4, out_5, out_6, out_7, out_8, out_9, out_10, out_11, bit0}), .dout(ram_1_dout));  // open: oe
  Register #(.width(4)) register_5 (.D(salUni), .clk(clock), .Q(register_5_q), .clr(reset));  // open: en
  // Multiplexer #(.select(4), .width(4)) multiplexer_3: pin names not known; wires that end beside it: 4'b0101, 4'b0000, salUni, multiplexer_3_p4, multiplexer_3_p5, multiplexer_3_p5
  and and_1 (and_1_out, comparator_3_eq, comparator_4_eq);
  Comparator #(.width(4)) comparator_3 (.a(register_5_q), .b(4'b0101), .eq(comparator_3_eq));  // open: gt, lt
  Comparator #(.width(4)) comparator_4 (.a(multiplexer_3_p4), .b(4'b0000), .eq(comparator_4_eq));  // open: gt, lt
  Comparator #(.width(10)) comparator_5 (
    .a({bit9, out_4, out_5, out_6, out_7, out_8, out_9, out_10, out_11, bit0}), .b(ram_1_dout),
    .gt(comparator_5_gt));  // open: eq, lt

  // Notes on the sheet:
  //   contador actual
  //   siguiente numero a mostrar
  //   en todos los mux, estos deciden cual es el 
endmodule

module contadorRecord (
  input  ENC,
  input  [3:0] Unidades,
  input  [3:0] Decenas,
  input  [3:0] Centenas,
  output bit0,
  output out_6,
  output out_7,
  output out_8,
  output [3:0] COut,
  output [3:0] DOut,
  output [3:0] Uout,
  output out_12,
  output out_13,
  output out_14,
  output out_15,
  output out_16,
  output bit9
);

  wire CLK_out, comparator_1_lt;
  wire [9:0] adder_1_out, multiplier_1_out, multiplier_2_out;
  wire [11:0] multiplexer_1_out;

  Multiplexer #(.width(12)) multiplexer_1 (
    .in0({COut, DOut, Uout}), .in1({Centenas, Decenas, Unidades}), .out(multiplexer_1_out),
    .sel(comparator_1_lt));
  RAM #(.addrWidth(2), .dataWidth(12)) ram_1 (
    .addr(2'b01), .we(comparator_1_lt), .oe(ENC), .clk(CLK_out), .din(multiplexer_1_out),
    .dout({COut, DOut, Uout}));
  Clock CLK (.out(CLK_out));
  Comparator #(.mode("unsigned"), .width(12)) comparator_1 (
    .a({COut, DOut, Uout}), .b({Centenas, Decenas, Unidades}), .lt(comparator_1_lt));  // open: gt, eq
  Multiplier #(.width(10)) multiplier_1 (.a(10'h64), .b({{6{1'b0}}, COut}), .out(multiplier_1_out));  // open: cin, cout
  Multiplier #(.width(10)) multiplier_2 (.a(10'ha), .b({{6{1'b0}}, DOut}), .out(multiplier_2_out));  // open: cin, cout
  Adder #(.width(10)) adder_1 (.a(multiplier_1_out), .b(multiplier_2_out), .out(adder_1_out));  // open: cin, cout
  Adder #(.width(10)) adder_2 (
    .a(adder_1_out), .b({{6{1'b0}}, Uout}),
    .out({bit9, out_16, out_15, out_14, out_13, out_12, out_8, out_7, out_6, bit0}));  // open: cin, cout

  // Notes on the sheet:
  //   hay que sobreescribir
endmodule

module ME (
  input  A,
  input  B,
  output PuertaA,
  output PuertaB
);

  wire and_1_out, and_2_out, and_3_out, and_4_out, CLK_out, not_1_out, not_2_out, not_3_out, not_4_out,
       not_5_out, not_6_out, not_7_out, or_1_out, or_2_out;

  not not_1 (not_1_out, A);
  not not_2 (not_2_out, PuertaA);
  not not_3 (not_3_out, PuertaB);
  not not_4 (not_4_out, PuertaA);
  not not_5 (not_5_out, PuertaB);
  not not_6 (not_6_out, PuertaA);
  not not_7 (not_7_out, B);
  and and_1 (and_1_out, PuertaA, not_1_out);
  and and_2 (and_2_out, A, not_2_out, not_3_out);
  and and_3 (and_3_out, not_4_out, not_5_out, B);
  and and_4 (and_4_out, not_6_out, PuertaB, not_7_out);
  or or_1 (or_1_out, and_1_out, and_2_out);
  or or_2 (or_2_out, and_3_out, and_4_out);
  D_Flip_Flop d_ff_1 (.D(or_1_out), .clk(CLK_out), .Q(PuertaA));  // open: Qn, preset, reset
  D_Flip_Flop d_ff_2 (.D(or_2_out), .clk(CLK_out), .Q(PuertaB));  // open: Qn, preset, reset
  Clock CLK (.out(CLK_out));

  // Notes on the sheet:
  //   Qb
  //   Qa
endmodule
