// Logisim project obComienzoContador.circ as structural Verilog: 3 circuits, main circuit main
module main (
  input  in_1,
  input  in_2,
  input  in_3
);

  wire clock_1_out, clock_2_out, clock_3_out, clock_4_out, contadortest_1_bit0, contadortest_1_bit9,
       contadortest_1_out_5, contadortest_1_out_6, contadortest_1_out_7, contadortest_1_out_8,
       contadortest_1_out_9, contadortest_1_out_10, contadortest_1_out_11, contadortest_1_out_12, et1, et2,
       et3, et4, et5, et6, et7, et8, et9, et10, et11, et12, et13, et14, et15, et16;
  wire [3:0] contadortest_1_salcent, contadortest_1_saldec, contadortest_1_saluni;
  wire [15:0] shift_register_1_p3, shift_register_3_p11;

  Clock clock_1 (.out(clock_1_out));
  Clock clock_2 (.out(clock_2_out));
  Clock clock_3 (.out(clock_3_out));
  // Shift_Register #(.length(16)) shift_register_1: pin names not known; wires that end beside it: clock_1_out, shift_register_1_p3[15], shift_register_1_p3[0], shift_register_1_p3[1], shift_register_1_p3[2], shift_register_1_p3[3], shift_register_1_p3[4], shift_register_1_p3[5], shift_register_1_p3[6], shift_register_1_p3[7]
  // Shift_Register #(.length(16)) shift_register_2: pin names not known; wires that end beside it: clock_2_out, et16, shift_register_1_p3[15], shift_register_1_p3[8], shift_register_1_p3[9], shift_register_1_p3[10], shift_register_1_p3[11], shift_register_1_p3[12], shift_register_1_p3[13], shift_register_1_p3[14], et1, et2, et3, et4, et5, et6, et7, et8
  // Shift_Register #(.length(16)) shift_register_3: pin names not known; wires that end beside it: clock_3_out, shift_register_3_p11[15], et16, et9, et10, et11, et12, et13, et14, et15, shift_register_3_p11[0], shift_register_3_p11[1], shift_register_3_p11[2], shift_register_3_p11[3], shift_register_3_p11[4], shift_register_3_p11[5], shift_register_3_p11[6], shift_register_3_p11[7], shift_register_3_p11[8], shift_register_3_p11[9], shift_register_3_p11[10], shift_register_3_p11[11]
  DotMatrix #(.inputtype("row"), .matrixcols(16), .matrixrows(8)) dotmatrix_1 (
    .row1(shift_register_1_p3),
    .row4({et1, et2, et3, et4, et5, et6, et7, et8, et9, et10, et11, et12, et13, et14, et15, et16}),
    .row6(shift_register_3_p11));  // open: row0, row2, row3, row5, row7
  Hex_Digit_Display hex_digit_display_1 (.value(contadortest_1_salcent));  // open: dp
  Hex_Digit_Display hex_digit_display_2 (.value(contadortest_1_saluni));  // open: dp
  Hex_Digit_Display hex_digit_display_3 (.value(contadortest_1_saldec));  // open: dp
  Clock clock_4 (.out(clock_4_out));
  contadorTest contadortest_1 (
    .salDec(contadortest_1_saldec), .salCent(contadortest_1_salcent), .salUni(contadortest_1_saluni),
    .resetUni(in_1), .resetCent(in_2), .resetDec(in_3), .bit9(contadortest_1_bit9),
    .out_5(contadortest_1_out_5), .out_6(contadortest_1_out_6), .out_7(contadortest_1_out_7),
    .out_8(contadortest_1_out_8), .out_9(contadortest_1_out_9), .out_10(contadortest_1_out_10),
    .out_11(contadortest_1_out_11), .out_12(contadortest_1_out_12), .bit0(contadortest_1_bit0));
  LED led_1 (.in(contadortest_1_bit9));
  LED led_2 (.in(contadortest_1_out_5));
  LED led_3 (.in(contadortest_1_out_6));
  LED led_4 (.in(contadortest_1_out_7));
  LED led_5 (.in(contadortest_1_out_8));
  LED led_6 (.in(contadortest_1_out_9));
  LED led_7 (.in(contadortest_1_out_10));
  LED led_8 (.in(contadortest_1_out_11));
  LED led_9 (.in(contadortest_1_out_12));
  LED led_10 (.in(contadortest_1_bit0));
endmodule

module contadorTest (
  input  resetUni,
  input  resetCent,
  input  resetDec,
  output bit9,
  output out_5,
  output out_6,
  output out_7,
  output out_8,
  output out_9,
  output out_10,
  output out_11,
  output out_12,
  output bit0,
  output [3:0] salDec,
  output [3:0] salCent,
  output [3:0] salUni
);

  wire and_1_out, and_2_out, clock_1_out, comparator_1_eq, comparator_2_eq, comparator_3_eq, comparator_4_eq,
       comparator_5_eq;
  wire [3:0] adder_2_out, adder_3_out, multiplexer_1_out, multiplexer_2_out, multiplexer_3_out;
  wire [9:0] adder_1_out;

  Clock clock_1 (.out(clock_1_out));
  Register #(.width(4)) register_1 (.D(multiplexer_1_out), .clk(and_1_out), .Q(salCent), .clr(resetCent));  // open: en
  Multiplexer #(.select(4), .width(4)) multiplexer_1 (
    .in0(4'b0001), .in1(4'b0010), .in2(4'b0011), .in3(4'b0100), .in4(4'b0101), .in5(4'b0110), .in6(4'b0111),
    .in7(4'b1000), .in8(4'b1001), .in9(4'b0000), .out(multiplexer_1_out), .sel(salCent));  // open: in10, in11, in12, in13, in14, in15
  Comparator #(.mode("unsigned"), .width(10)) comparator_1 (
    .a({bit9, out_5, out_6, out_7, out_8, out_9, out_10, out_11, out_12, bit0}), .b(10'h3e3),
    .eq(comparator_1_eq));  // open: gt, lt
  Adder #(.width(10)) adder_1 (
    .a({bit9, out_5, out_6, out_7, out_8, out_9, out_10, out_11, out_12, bit0}), .b(10'h5), .out(adder_1_out));  // open: cin, cout
  Register #(.width(4)) register_2 (.D(multiplexer_2_out), .clk(and_2_out), .Q(salDec), .clr(resetDec));  // open: en
  Register #(.width(10)) register_3 (
    .D(adder_1_out), .clk(clock_1_out),
    .Q({bit9, out_5, out_6, out_7, out_8, out_9, out_10, out_11, out_12, bit0}), .clr(comparator_1_eq));  // open: en
  and and_1 (and_1_out, comparator_3_eq, comparator_2_eq);
  Comparator #(.width(4)) comparator_2 (.a(4'b0000), .b(salDec), .eq(comparator_2_eq));  // open: gt, lt
  Adder #(.width(4)) adder_2 (.a(4'b0000), .b(salDec), .out(adder_2_out));  // open: cin, cout
  Multiplexer #(.select(4), .width(4)) multiplexer_2 (
    .in0(4'b0001), .in1(4'b0010), .in2(4'b0011), .in3(4'b0100), .in4(4'b0101), .in5(4'b0110), .in6(4'b0111),
    .in7(4'b1000), .in8(4'b1001), .in9(4'b0000), .out(multiplexer_2_out), .sel(salDec));  // open: in10, in11, in12, in13, in14, in15
  Comparator #(.width(4)) comparator_3 (.a(adder_2_out), .b(4'b0000), .eq(comparator_3_eq));  // open: gt, lt
  Register #(.width(4)) register_4 (.D(multiplexer_3_out), .clk(clock_1_out), .Q(salUni), .clr(resetUni));  // open: en
  Comparator #(.width(4)) comparator_4 (.a(4'b0000), .b(salUni), .eq(comparator_4_eq));  // open: gt, lt
  Adder #(.width(4)) adder_3 (.a(4'b0000), .b(salUni), .out(adder_3_out));  // open: cin, cout
  Multiplexer #(.select(4), .width(4)) multiplexer_3 (
    .in0(4'b0101), .in5(4'b0000), .out(multiplexer_3_out), .sel(salUni));  // open: in1, in2, in3, in4, in6, in7, in8, in9, in10, in11, in12, in13, in14, in15
  and and_2 (and_2_out, comparator_4_eq, comparator_5_eq);
  Comparator #(.width(4)) comparator_5 (.a(adder_3_out), .b(4'b0000), .eq(comparator_5_eq));  // open: gt, lt

  // Notes on the sheet:
  //   siguiente numero a mostrar
  //   en todos los mux, estos deciden cual es el 
endmodule

module contador2JK (
  input  in_1
);

  wire clock_1_out, j_k_ff_1_q, j_k_ff_1_qn, j_k_ff_2_q, j_k_ff_2_qn, j_k_ff_3_q, j_k_ff_3_qn, j_k_ff_4_q;

  Clock clock_1 (.out(clock_1_out));
  J_K_Flip_Flop j_k_ff_1 (
    .J(in_1), .K(in_1), .clk(clock_1_out), .Q(j_k_ff_1_q), .Qn(j_k_ff_1_qn));  // open: preset, reset
  J_K_Flip_Flop j_k_ff_2 (
    .J(in_1), .K(in_1), .clk(j_k_ff_1_qn), .Q(j_k_ff_2_q), .Qn(j_k_ff_2_qn));  // open: preset, reset
  J_K_Flip_Flop j_k_ff_3 (
    .J(in_1), .K(in_1), .clk(j_k_ff_2_qn), .Q(j_k_ff_3_q), .Qn(j_k_ff_3_qn));  // open: preset, reset
  J_K_Flip_Flop j_k_ff_4 (.J(in_1), .K(in_1), .clk(j_k_ff_3_qn), .Q(j_k_ff_4_q));  // open: Qn, preset, reset
  _7_Segment_Display u_7_segment_display_1 ();  // open: g, f, a, b, e, d, c, dp
endmodule
