// Logisim project obJugadorMovsXYcirc.circ as structural Verilog: 6 circuits, main circuit main
module main (
  output [3:0] pos_x,
  output [2:0] pos_y
);

  wire clock_1_out, clock_2_out, clock_3_out, der_out, down_out, et1, et2, et3, et4, et5, et6, et7, et8, et9,
       et10, et11, et12, et13, et14, et15, et16, izq_out, up_out;
  wire [15:0] dibujarjugador_1_filajugador0, dibujarjugador_1_filajugador1, dibujarjugador_1_filajugador2,
       dibujarjugador_1_filajugador3, dibujarjugador_1_filajugador4, dibujarjugador_1_filajugador5,
       dibujarjugador_1_filajugador6, dibujarjugador_1_filajugador7, shift_register_1_p3,
       shift_register_3_p12;

  Clock clock_1 (.out(clock_1_out));
  Clock clock_2 (.out(clock_2_out));
  Clock clock_3 (.out(clock_3_out));
  // Shift_Register #(.length(16)) shift_register_1: pin names not known; wires that end beside it: clock_1_out, shift_register_1_p3[15], shift_register_1_p3[0], shift_register_1_p3[1], shift_register_1_p3[2], shift_register_1_p3[3], shift_register_1_p3[4], shift_register_1_p3[5], shift_register_1_p3[6], shift_register_1_p3[7]
  // Shift_Register #(.length(16)) shift_register_2: pin names not known; wires that end beside it: clock_2_out, et16, shift_register_1_p3[15], shift_register_1_p3[8], shift_register_1_p3[9], shift_register_1_p3[10], shift_register_1_p3[11], shift_register_1_p3[12], shift_register_1_p3[13], shift_register_1_p3[14], et1, et2, et3, et4, et5, et6, et7
  // Shift_Register #(.length(16)) shift_register_3: pin names not known; wires that end beside it: clock_3_out, shift_register_3_p12[15], et16, et8, et9, et10, et11, et12, et13, et14, et15, shift_register_3_p12[0], shift_register_3_p12[1], shift_register_3_p12[2], shift_register_3_p12[3], shift_register_3_p12[4], shift_register_3_p12[5], shift_register_3_p12[6], shift_register_3_p12[7], shift_register_3_p12[8], shift_register_3_p12[9], shift_register_3_p12[10], shift_register_3_p12[11]
  DotMatrix #(.inputtype("row"), .matrixcols(16), .matrixrows(8)) dotmatrix_1 (
    .row1(shift_register_1_p3),
    .row4({et1, et2, et3, et4, et5, et6, et7, et8, et9, et10, et11, et12, et13, et14, et15, et16}),
    .row6(shift_register_3_p12));  // open: row0, row2, row3, row5, row7
  Decoder #(.select(3)) decoder_1 ();  // open: out0, out1, out2, out3, out4, out5, out6, out7, sel, en
  Button izq (.out(izq_out));
  Button up (.out(up_out));
  Button der (.out(der_out));
  Button down (.out(down_out));
  movX movx_1 (.left(izq_out), .right(der_out), .posExit(pos_x));
  movY movy_1 (.down(down_out), .up(up_out), .posExit(pos_y));
  dibujarJugador dibujarjugador_1 (
    .PosX(pos_x), .PosY(pos_y), .filaJugador0(dibujarjugador_1_filajugador0),
    .filaJugador1(dibujarjugador_1_filajugador1), .filaJugador2(dibujarjugador_1_filajugador2),
    .filaJugador3(dibujarjugador_1_filajugador3), .filaJugador4(dibujarjugador_1_filajugador4),
    .filaJugador5(dibujarjugador_1_filajugador5), .filaJugador6(dibujarjugador_1_filajugador6),
    .filaJugador7(dibujarjugador_1_filajugador7));
  DotMatrix #(.inputtype("row"), .matrixcols(16), .matrixrows(8)) dotmatrix_2 (
    .row0(dibujarjugador_1_filajugador0), .row1(dibujarjugador_1_filajugador1),
    .row2(dibujarjugador_1_filajugador2), .row3(dibujarjugador_1_filajugador3),
    .row4(dibujarjugador_1_filajugador4), .row5(dibujarjugador_1_filajugador5),
    .row6(dibujarjugador_1_filajugador6), .row7(dibujarjugador_1_filajugador7));
endmodule

module movX (
  input  left,
  input  right,
  output [3:0] posExit
);

  wire clock_1_out, comparator_1_gt, comparator_2_lt;
  wire [1:0] and_2_out;
  wire [3:0] adder_1_out, register_1_q, subtractor_1_out;

  Clock clock_1 (.out(clock_1_out));
  Register #(.width(4)) register_1 (.D(posExit), .clk(clock_1_out), .Q(register_1_q));  // open: en, clr
  Comparator #(.mode("unsigned"), .width(4)) comparator_1 (
    .a(register_1_q), .b(4'b0000), .gt(comparator_1_gt));  // open: eq, lt
  Comparator #(.mode("unsigned"), .width(4)) comparator_2 (
    .a(register_1_q), .b(4'b1111), .lt(comparator_2_lt));  // open: gt, eq
  Adder #(.width(4)) adder_1 (.a(register_1_q), .b(4'b0001), .out(adder_1_out));  // open: cin, cout
  Subtractor #(.width(4)) subtractor_1 (.a(register_1_q), .b(4'b0001), .out(subtractor_1_out));  // open: bin, bout
  and and_1 (and_2_out[1], left, comparator_1_gt);
  and and_2 (and_2_out[0], right, comparator_2_lt);
  Multiplexer #(.select(2), .width(4)) multiplexer_1 (
    .in0(register_1_q), .in1(adder_1_out), .in2(subtractor_1_out), .in3(register_1_q), .out(posExit),
    .sel(and_2_out));

  // Notes on the sheet:
  //   x+1 (der)
  //    (01 der)
  //   x-1 (izq)
  //   codificador
  //   aca decide si puede moverse o no
  //   (10 izq)
endmodule

module movY (
  input  down,
  input  up,
  output [2:0] posExit
);

  wire clock_1_out, comparator_1_gt, comparator_2_lt;
  wire [1:0] and_2_out;
  wire [2:0] adder_1_out, register_1_q, subtractor_1_out;

  Clock clock_1 (.out(clock_1_out));
  Register #(.width(3)) register_1 (.D(posExit), .clk(clock_1_out), .Q(register_1_q));  // open: en, clr
  Comparator #(.mode("unsigned"), .width(3)) comparator_1 (
    .a(register_1_q), .b(3'b000), .gt(comparator_1_gt));  // open: eq, lt
  Comparator #(.mode("unsigned"), .width(3)) comparator_2 (
    .a(register_1_q), .b(3'b111), .lt(comparator_2_lt));  // open: gt, eq
  Adder #(.width(3)) adder_1 (.a(register_1_q), .b(3'b001), .out(adder_1_out));  // open: cin, cout
  Subtractor #(.width(3)) subtractor_1 (.a(register_1_q), .b(3'b001), .out(subtractor_1_out));  // open: bin, bout
  and and_1 (and_2_out[1], down, comparator_1_gt);
  and and_2 (and_2_out[0], up, comparator_2_lt);
  Multiplexer #(.select(2), .width(3)) multiplexer_1 (
    .in0(register_1_q), .in1(adder_1_out), .in2(subtractor_1_out), .in3(register_1_q), .out(posExit),
    .sel(and_2_out));

  // Notes on the sheet:
  //   x+1 (der)
  //    (01 der)
  //   x-1 (izq)
  //   codificador
  //   aca decide si puede moverse o no
  //   (10 izq)
endmodule

module contadorTest (
  input  resetUni,
  input  resetCent,
  input  resetDec,
  output bit9,
  output out_5,
  output out_6,
  output out_7,
  output out_8,
  output out_9,
  output out_10,
  output out_11,
  output out_12,
  output bit0,
  output [3:0] salDec,
  output [3:0] salCent,
  output [3:0] salUni
);

  wire and_1_out, and_2_out, clock_1_out, comparator_1_eq, comparator_2_eq, comparator_3_eq, comparator_4_eq,
       comparator_5_eq;
  wire [3:0] adder_2_out, adder_3_out, multiplexer_1_out, multiplexer_2_out, multiplexer_3_out;
  wire [9:0] adder_1_out;

  Clock clock_1 (.out(clock_1_out));
  Register #(.width(4)) register_1 (.D(multiplexer_1_out), .clk(and_1_out), .Q(salCent), .clr(resetCent));  // open: en
  Multiplexer #(.select(4), .width(4)) multiplexer_1 (
    .in0(4'b0001), .in1(4'b0010), .in2(4'b0011), .in3(4'b0100), .in4(4'b0101), .in5(4'b0110), .in6(4'b0111),
    .in7(4'b1000), .in8(4'b1001), .in9(4'b0000), .out(multiplexer_1_out), .sel(salCent));  // open: in10, in11, in12, in13, in14, in15
  Comparator #(.mode("unsigned"), .width(10)) comparator_1 (
    .a({bit9, out_5, out_6, out_7, out_8, out_9, out_10, out_11, out_12, bit0}), .b(10'h3e3),
    .eq(comparator_1_eq));  // open: gt, lt
  Adder #(.width(10)) adder_1 (
    .a({bit9, out_5, out_6, out_7, out_8, out_9, out_10, out_11, out_12, bit0}), .b(10'h5), .out(adder_1_out));  // open: cin, cout
  Register #(.width(4)) register_2 (.D(multiplexer_2_out), .clk(and_2_out), .Q(salDec), .clr(resetDec));  // open: en
  Register #(.width(10)) register_3 (
    .D(adder_1_out), .clk(clock_1_out),
    .Q({bit9, out_5, out_6, out_7, out_8, out_9, out_10, out_11, out_12, bit0}), .clr(comparator_1_eq));  // open: en
  and and_1 (and_1_out, comparator_3_eq, comparator_2_eq);
  Comparator #(.width(4)) comparator_2 (.a(4'b0000), .b(salDec), .eq(comparator_2_eq));  // open: gt, lt
  Adder #(.width(4)) adder_2 (.a(4'b0000), .b(salDec), .out(adder_2_out));  // open: cin, cout
  Multiplexer #(.select(4), .width(4)) multiplexer_2 (
    .in0(4'b0001), .in1(4'b0010), .in2(4'b0011), .in3(4'b0100), .in4(4'b0101), .in5(4'b0110), .in6(4'b0111),
    .in7(4'b1000), .in8(4'b1001), .in9(4'b0000), .out(multiplexer_2_out), .sel(salDec));  // open: in10, in11, in12, in13, in14, in15
  Comparator #(.width(4)) comparator_3 (.a(adder_2_out), .b(4'b0000), .eq(comparator_3_eq));  // open: gt, lt
  Register #(.width(4)) register_4 (.D(multiplexer_3_out), .clk(clock_1_out), .Q(salUni), .clr(resetUni));  // open: en
  Comparator #(.width(4)) comparator_4 (.a(4'b0000), .b(salUni), .eq(comparator_4_eq));  // open: gt, lt
  Adder #(.width(4)) adder_3 (.a(4'b0000), .b(salUni), .out(adder_3_out));  // open: cin, cout
  Multiplexer #(.select(4), .width(4)) multiplexer_3 (
    .in0(4'b0101), .in5(4'b0000), .out(multiplexer_3_out), .sel(salUni));  // open: in1, in2, in3, in4, in6, in7, in8, in9, in10, in11, in12, in13, in14, in15
  and and_2 (and_2_out, comparator_4_eq, comparator_5_eq);
  Comparator #(.width(4)) comparator_5 (.a(adder_3_out), .b(4'b0000), .eq(comparator_5_eq));  // open: gt, lt

  // Notes on the sheet:
  //   siguiente numero a mostrar
  //   en todos los mux, estos deciden cual es el 
endmodule

module contador2JK (
  input  in_1
);

  wire clock_1_out, j_k_ff_1_q, j_k_ff_1_qn, j_k_ff_2_q, j_k_ff_2_qn, j_k_ff_3_q, j_k_ff_3_qn, j_k_ff_4_q;

  Clock clock_1 (.out(clock_1_out));
  J_K_Flip_Flop j_k_ff_1 (
    .J(in_1), .K(in_1), .clk(clock_1_out), .Q(j_k_ff_1_q), .Qn(j_k_ff_1_qn));  // open: preset, reset
  J_K_Flip_Flop j_k_ff_2 (
    .J(in_1), .K(in_1), .clk(j_k_ff_1_qn), .Q(j_k_ff_2_q), .Qn(j_k_ff_2_qn));  // open: preset, reset
  J_K_Flip_Flop j_k_ff_3 (
    .J(in_1), .K(in_1), .clk(j_k_ff_2_qn), .Q(j_k_ff_3_q), .Qn(j_k_ff_3_qn));  // open: preset, reset
  J_K_Flip_Flop j_k_ff_4 (.J(in_1), .K(in_1), .clk(j_k_ff_3_qn), .Q(j_k_ff_4_q));  // open: Qn, preset, reset
  _7_Segment_Display u_7_segment_display_1 ();  // open: g, f, a, b, e, d, c, dp
endmodule

module dibujarJugador (
  input  [3:0] PosX,
  input  [2:0] PosY,
  output [15:0] filaJugador0,
  output [15:0] filaJugador1,
  output [15:0] filaJugador2,
  output [15:0] filaJugador3,
  output [15:0] filaJugador4,
  output [15:0] filaJugador5,
  output [15:0] filaJugador6,
  output [15:0] filaJugador7
);

  wire [3:0] subtractor_1_out;
  wire [15:0] shifter_1_out;

  Subtractor #(.width(4)) subtractor_1 (.a(4'b1111), .b(PosX), .out(subtractor_1_out));  // open: bin, bout
  Shifter #(.width(16)) shifter_1 (.in(16'h1), .\dist (subtractor_1_out), .out(shifter_1_out));
  Demultiplexer #(.select(3), .width(16)) demultiplexer_1 (
    .out0(filaJugador7), .out1(filaJugador6), .out2(filaJugador5), .out3(filaJugador4), .out4(filaJugador3),
    .out5(filaJugador2), .out6(filaJugador1), .out7(filaJugador0), .in(shifter_1_out), .sel(PosY));

  // Other names for the same wires on the sheet: fj0[15:0] = filaJugador7; fj1[15:0] = filaJugador6;
  //   fj2[15:0] = filaJugador5; fj3[15:0] = filaJugador4; fj4[15:0] = filaJugador3; fj5[15:0] = filaJugador2;
  //   fj6[15:0] = filaJugador1; fj7[15:0] = filaJugador0
endmodule
