// Logisim project contadorRecord.circ as structural Verilog: 1 circuit, main circuit contadorRecord
module contadorRecord (
  input  b1,
  input  b2,
  input  ENC,
  input  b3,
  input  b4,
  input  b5,
  input  b6,
  input  b7,
  input  b8,
  input  b9,
  input  b10,
  input  [3:0] Unidades,
  input  [3:0] Decenas,
  input  [3:0] Centenas,
  output [3:0] COut,
  output [3:0] DOut,
  output [3:0] Uout
);

  wire CLK_out, comparator_1_lt;
  wire [9:0] adder_1_out, multiplier_1_out, multiplier_2_out;
  wire [11:0] multiplexer_1_out;

  Multiplexer #(.width(12)) multiplexer_1 (
    .in0({COut, DOut, Uout}), .in1({Centenas, Decenas, Unidades}), .out(multiplexer_1_out),
    .sel(comparator_1_lt));
  RAM #(.addrWidth(2), .dataWidth(12)) ram_1 (
    .addr(2'b01), .we(comparator_1_lt), .oe(ENC), .clk(CLK_out), .din(multiplexer_1_out),
    .dout({COut, DOut, Uout}));
  Clock CLK (.out(CLK_out));
  Comparator #(.mode("unsigned"), .width(12)) comparator_1 (
    .a({COut, DOut, Uout}), .b({Centenas, Decenas, Unidades}), .lt(comparator_1_lt));  // open: gt, eq
  Multiplier #(.width(10)) multiplier_1 (.a(10'h64), .b({{6{1'b0}}, COut}), .out(multiplier_1_out));  // open: cin, cout
  Multiplier #(.width(10)) multiplier_2 (.a(10'ha), .b({{6{1'b0}}, DOut}), .out(multiplier_2_out));  // open: cin, cout
  Adder #(.width(10)) adder_1 (.a(multiplier_1_out), .b(multiplier_2_out), .out(adder_1_out));  // open: cin, cout
  Adder #(.width(10)) adder_2 (
    .a(adder_1_out), .b({{6{1'b0}}, Uout}), .out({b10, b9, b8, b7, b6, b5, b4, b3, b2, b1}));  // open: cin, cout

  // Notes on the sheet:
  //   hay que sobreescribir
  //   QUEDA SEPARARLOS EN OUTPUTS(?)
endmodule
