// Logisim project mainAlDia - Contador.circ as structural Verilog: 4 circuits, main circuit main
module main (
);

  wire and_1_out, and_2_out, and_7_out, and_8_out, button_1_out, button_2_out, button_3_out, button_4_out,
       clock_1_out, clock_2_out, comparator_1_eq, comparator_2_eq, comparator_3_eq, comparator_4_eq,
       comparator_5_eq, comparator_6_eq, comparator_7_eq, comparator_8_eq, comparator_9_gt, comparator_10_eq,
       contador_1_bit0, contador_1_bit9, contador_1_out_4, contador_1_out_5, contador_1_out_6,
       contador_1_out_7, contador_1_out_8, contador_1_out_9, contador_1_out_10, contador_1_out_11, d_ff_1_q,
       et1, et2, et3, et4, et5, et6, et7, et8, et9, et10, et11, et12, et13, et14, et15, et16, not_4_out,
       not_5_out, or_1_out, or_2_out, or_3_out, or_4_out, or_9_out, por_1_out, por_2_out, register_1_q, Rst,
       s_r_ff_1_q, shift_register_1_p1, shift_register_2_p10, shift_register_3_p10;
  wire [2:0] counter_1_q, movy_1_posexit;
  wire [3:0] contador_1_salcent, contador_1_saldec, contador_1_saluni, movx_1_posexit;
  wire [15:0] and_3_out, and_4_out, and_5_out, decoder_1_out15, multiplexer_1_out, multiplexer_2_out,
       multiplexer_3_out, multiplexer_4_out, multiplexer_5_out, multiplexer_6_out, multiplexer_7_out,
       multiplexer_8_out, multiplexer_9_out, multiplexer_10_out, multiplexer_11_out, or_5_out, or_6_out,
       or_7_out, or_8_out, shift_register_1_p13, shift_register_3_p33;

  POR por_1 (.out(por_1_out));
  or or_1 (or_1_out, Rst, por_1_out);
  or or_2 (or_2_out, or_1_out, button_4_out);
  or or_3 (or_3_out, button_3_out, or_1_out);
  movX movx_1 (.left(button_1_out), .right(or_2_out), .reset(or_1_out), .posExit(movx_1_posexit));
  movY movy_1 (.down(button_3_out), .up(button_2_out), .reset(or_3_out), .posExit(movy_1_posexit));
  Decoder #(.select(4)) decoder_1 (
    .out0(decoder_1_out15[15]), .out1(decoder_1_out15[14]), .out2(decoder_1_out15[13]),
    .out3(decoder_1_out15[12]), .out4(decoder_1_out15[11]), .out5(decoder_1_out15[10]),
    .out6(decoder_1_out15[9]), .out7(decoder_1_out15[8]), .out8(decoder_1_out15[7]),
    .out9(decoder_1_out15[6]), .out10(decoder_1_out15[5]), .out11(decoder_1_out15[4]),
    .out12(decoder_1_out15[3]), .out13(decoder_1_out15[2]), .out14(decoder_1_out15[1]),
    .out15(decoder_1_out15[0]), .sel(movx_1_posexit));  // open: en
  Clock clock_1 (.out(clock_1_out));
  and and_1 (and_1_out, not_4_out, clock_1_out);
  POR #(.porsize(1)) por_2 (.out(por_2_out));
  // Shift_Register #(.length(16)) shift_register_1: pin names not known; wires that end beside it: shift_register_1_p1, and_1_out, shift_register_1_p13[15], 1'b1, 1'b0, 1'b0, 1'b0, 1'b1, 1'b1, 1'b0, 1'b1, por_2_out, shift_register_1_p13[0], shift_register_1_p13[1], shift_register_1_p13[2], shift_register_1_p13[3], shift_register_1_p13[4], shift_register_1_p13[5], shift_register_1_p13[6], shift_register_1_p13[7]
  not not_1 (shift_register_1_p1, por_2_out);
  // Shift_Register #(.length(16)) shift_register_2: pin names not known; wires that end beside it: 1'b0, 1'b1, 1'b0, 1'b0, 1'b0, 1'b1, 1'b0, 1'b1, por_2_out, shift_register_2_p10, and_1_out, et16, 1'b0, 1'b1, 1'b0, 1'b1, 1'b1, 1'b1, 1'b0, 1'b0, shift_register_1_p13[15], shift_register_1_p13[8], shift_register_1_p13[9], shift_register_1_p13[10], shift_register_1_p13[11], shift_register_1_p13[12], shift_register_1_p13[13], shift_register_1_p13[14], et1, et2, et3, et4, et5, et6, et7, et8
  not not_2 (shift_register_2_p10, por_2_out);
  // Shift_Register #(.length(16)) shift_register_3: pin names not known; wires that end beside it: 1'b0, 1'b0, 1'b0, 1'b1, 1'b0, 1'b1, 1'b0, 1'b0, por_2_out, shift_register_3_p10, and_1_out, shift_register_3_p33[15], 1'b0, 1'b1, 1'b0, 1'b1, 1'b0, 1'b0, 1'b0, 1'b1, 1'b1, 1'b0, 1'b0, 1'b0, et16, et9, et10, et11, et12, et13, et14, et15, shift_register_3_p33[0], shift_register_3_p33[1], shift_register_3_p33[2], shift_register_3_p33[3], shift_register_3_p33[4], shift_register_3_p33[5], shift_register_3_p33[6], shift_register_3_p33[7], shift_register_3_p33[8], shift_register_3_p33[9], shift_register_3_p33[10], shift_register_3_p33[11]
  not not_3 (shift_register_3_p10, por_2_out);
  and and_2 (and_2_out, s_r_ff_1_q, or_4_out);
  Comparator #(.mode("unsigned"), .width(3)) comparator_1 (
    .a(movy_1_posexit), .b(3'b111), .eq(comparator_1_eq));  // open: gt, lt
  Comparator #(.mode("unsigned"), .width(3)) comparator_2 (
    .a(movy_1_posexit), .b(3'b110), .eq(comparator_2_eq));  // open: gt, lt
  Comparator #(.mode("unsigned"), .width(3)) comparator_3 (
    .a(movy_1_posexit), .b(3'b101), .eq(comparator_3_eq));  // open: gt, lt
  Comparator #(.mode("unsigned"), .width(3)) comparator_4 (
    .a(movy_1_posexit), .b(3'b100), .eq(comparator_4_eq));  // open: gt, lt
  Comparator #(.mode("unsigned"), .width(3)) comparator_5 (
    .a(movy_1_posexit), .b(3'b011), .eq(comparator_5_eq));  // open: gt, lt
  Comparator #(.mode("unsigned"), .width(3)) comparator_6 (
    .a(movy_1_posexit), .b(3'b010), .eq(comparator_6_eq));  // open: gt, lt
  Comparator #(.mode("unsigned"), .width(3)) comparator_7 (
    .a(movy_1_posexit), .b(3'b001), .eq(comparator_7_eq));  // open: gt, lt
  Comparator #(.mode("unsigned"), .width(3)) comparator_8 (
    .a(movy_1_posexit), .b(3'b000), .eq(comparator_8_eq));  // open: gt, lt
  S_R_Flip_Flop s_r_ff_1 (
    .S(comparator_1_eq), .R(and_2_out), .clk(comparator_1_eq), .Q(s_r_ff_1_q), .reset(and_2_out));  // open: Qn, preset
  Multiplexer #(.width(16)) multiplexer_1 (
    .in0({16{1'b0}}), .in1(decoder_1_out15), .out(multiplexer_1_out), .sel(comparator_1_eq));
  Multiplexer #(.width(16)) multiplexer_2 (
    .in0({16{1'b0}}), .in1(decoder_1_out15), .out(multiplexer_2_out), .sel(comparator_2_eq));
  Multiplexer #(.width(16)) multiplexer_3 (
    .in0({16{1'b0}}), .in1(decoder_1_out15), .out(multiplexer_3_out), .sel(comparator_3_eq));
  Multiplexer #(.width(16)) multiplexer_4 (
    .in0({16{1'b0}}), .in1(decoder_1_out15), .out(multiplexer_4_out), .sel(comparator_4_eq));
  Multiplexer #(.width(16)) multiplexer_5 (
    .in0({16{1'b0}}), .in1(decoder_1_out15), .out(multiplexer_5_out), .sel(comparator_5_eq));
  Multiplexer #(.width(16)) multiplexer_6 (
    .in0({16{1'b0}}), .in1(decoder_1_out15), .out(multiplexer_6_out), .sel(comparator_6_eq));
  Multiplexer #(.width(16)) multiplexer_7 (
    .in0({16{1'b0}}), .in1(decoder_1_out15), .out(multiplexer_7_out), .sel(comparator_7_eq));
  Multiplexer #(.width(16)) multiplexer_8 (
    .in0({16{1'b0}}), .in1(decoder_1_out15), .out(multiplexer_8_out), .sel(comparator_8_eq));
  Multiplexer #(.width(16)) multiplexer_9 (
    .in0(shift_register_1_p13), .in1({16{1'b0}}), .out(multiplexer_9_out), .sel(register_1_q));
  Multiplexer #(.width(16)) multiplexer_10 (
    .in0({et1, et2, et3, et4, et5, et6, et7, et8, et9, et10, et11, et12, et13, et14, et15, et16}),
    .in1({16{1'b0}}), .out(multiplexer_10_out), .sel(register_1_q));
  or or_4 (or_4_out, comparator_8_eq, s_r_ff_1_q);
  assign or_5_out = multiplexer_2_out | multiplexer_9_out;  // OR_Gate or_5, 16 bits wide
  assign or_6_out = multiplexer_5_out | multiplexer_10_out;  // OR_Gate or_6, 16 bits wide
  assign or_7_out = multiplexer_7_out | multiplexer_11_out;  // OR_Gate or_7, 16 bits wide
  Multiplexer #(.width(16)) multiplexer_11 (
    .in0(shift_register_3_p33), .in1({16{1'b0}}), .out(multiplexer_11_out), .sel(register_1_q));
  contador contador_1 (
    .clock(or_4_out), .reset(comparator_10_eq), .bit9(contador_1_bit9), .out_4(contador_1_out_4),
    .out_5(contador_1_out_5), .out_6(contador_1_out_6), .out_7(contador_1_out_7), .out_8(contador_1_out_8),
    .out_9(contador_1_out_9), .out_10(contador_1_out_10), .out_11(contador_1_out_11), .bit0(contador_1_bit0),
    .salDec(contador_1_saldec), .salCent(contador_1_salcent), .salUni(contador_1_saluni));
  DotMatrix #(.inputtype("row"), .matrixcols(16), .matrixrows(8)) dotmatrix_1 (
    .row0(multiplexer_1_out), .row1(or_5_out), .row2(multiplexer_3_out), .row3(multiplexer_4_out),
    .row4(or_6_out), .row5(multiplexer_6_out), .row6(or_7_out), .row7(multiplexer_8_out));
  LED led_1 (.in(contador_1_bit9));
  LED led_2 (.in(contador_1_out_4));
  LED led_3 (.in(contador_1_out_5));
  LED led_4 (.in(contador_1_out_6));
  Hex_Digit_Display hex_digit_display_1 (.value(contador_1_salcent));  // open: dp
  Button button_1 (.out(button_1_out));
  LED led_5 (.in(contador_1_out_7));
  LED led_6 (.in(contador_1_out_8));
  LED led_7 (.in(contador_1_out_9));
  LED led_8 (.in(contador_1_out_10));
  Hex_Digit_Display hex_digit_display_2 (.value(contador_1_saldec));  // open: dp
  Button button_2 (.out(button_2_out));
  Button button_3 (.out(button_3_out));
  LED led_9 (.in(contador_1_out_11));
  LED led_10 (.in(contador_1_bit0));
  Hex_Digit_Display hex_digit_display_3 (.value(contador_1_saluni));  // open: dp
  Button button_4 (.out(button_4_out));
  LED led_11 ();  // open: in
  LED led_12 ();  // open: in
  LED led_13 ();  // open: in
  Hex_Digit_Display hex_digit_display_4 ();  // open: value, dp
  LED led_14 ();  // open: in
  LED led_15 ();  // open: in
  LED led_16 ();  // open: in
  LED led_17 ();  // open: in
  Hex_Digit_Display hex_digit_display_5 ();  // open: value, dp
  assign and_3_out = multiplexer_2_out & multiplexer_9_out;  // AND_Gate and_3, 16 bits wide
  assign and_4_out = multiplexer_10_out & multiplexer_5_out;  // AND_Gate and_4, 16 bits wide
  assign and_5_out = multiplexer_11_out & multiplexer_7_out;  // AND_Gate and_5, 16 bits wide
  LED led_18 ();  // open: in
  LED led_19 ();  // open: in
  LED led_20 ();  // open: in
  Hex_Digit_Display hex_digit_display_6 ();  // open: value, dp
  assign or_8_out = and_3_out | and_4_out | and_5_out;  // OR_Gate or_8, 16 bits wide
  Comparator #(.mode("unsigned"), .width(16)) comparator_9 (
    .a(or_8_out), .b({16{1'b0}}), .gt(comparator_9_gt));  // open: eq, lt
  LED led_21 (.in(comparator_9_gt));
  or or_9 (or_9_out, comparator_9_gt, d_ff_1_q);
  Clock clock_2 (.out(clock_2_out));
  not not_4 (not_4_out, d_ff_1_q);
  D_Flip_Flop d_ff_1 (.D(or_9_out), .clk(clock_2_out), .Q(d_ff_1_q));  // open: Qn, preset, reset
  and and_6 (Rst, comparator_10_eq, d_ff_1_q);
  not not_5 (not_5_out, register_1_q);
  Register #(.width(1)) register_1 (.D(and_7_out), .clk(clock_2_out), .Q(register_1_q));  // open: en, clr
  and and_7 (and_7_out, not_5_out, d_ff_1_q);
  and and_8 (and_8_out, register_1_q, clock_2_out);
  Counter #(.max('h7), .width(3)) counter_1 (.clk(and_8_out), .Q(counter_1_q));  // open: clr, load, up, count, D, carry
  Comparator #(.width(3)) comparator_10 (.a(3'b110), .b(counter_1_q), .eq(comparator_10_eq));  // open: gt, lt

  // Notes on the sheet:
  //   Salida de posicionY
  //   por alguna razon tuve que conectar
  //   el reset de abajo tambien para que ande
  //   porque sino contaba los puntos dos veces
  //   Puntaje actual
  //   Puntaje record
  //   Flag de Colisión
  //   Registro de Perder
  //   Cuenta 6 ticks dsp de perder, luego reinicio.
endmodule

module movX (
  input  left,
  input  right,
  input  reset,
  output [3:0] posExit
);

  wire comparator_1_gt, comparator_2_lt, nor_1_out;
  wire [1:0] and_2_out;
  wire [3:0] adder_1_out, multiplexer_1_out, multiplexer_2_out, subtractor_1_out;

  Register #(.width(4)) register_1 (.D(multiplexer_2_out), .clk(nor_1_out), .Q(posExit));  // open: en, clr
  nor nor_1 (nor_1_out, left, right);
  Comparator #(.mode("unsigned"), .width(4)) comparator_1 (
    .a(posExit), .b(4'b0000), .gt(comparator_1_gt));  // open: eq, lt
  Comparator #(.mode("unsigned"), .width(4)) comparator_2 (
    .a(posExit), .b(4'b1111), .lt(comparator_2_lt));  // open: gt, eq
  Adder #(.width(4)) adder_1 (.a(posExit), .b(4'b0001), .out(adder_1_out));  // open: cin, cout
  Subtractor #(.width(4)) subtractor_1 (.a(posExit), .b(4'b0001), .out(subtractor_1_out));  // open: bin, bout
  and and_1 (and_2_out[1], left, comparator_1_gt);
  and and_2 (and_2_out[0], right, comparator_2_lt);
  Multiplexer #(.select(2), .width(4)) multiplexer_1 (
    .in0(posExit), .in1(adder_1_out), .in2(subtractor_1_out), .in3(posExit), .out(multiplexer_1_out),
    .sel(and_2_out));
  Multiplexer #(.width(4)) multiplexer_2 (.in0(multiplexer_1_out), .in1(4'b0111), .out(multiplexer_2_out), .sel(reset));

  // Notes on the sheet:
  //   x+1 (der)
  //    (01 der)
  //   x-1 (izq)
  //   codificador
  //   aca decide si puede moverse o no
  //   (10 izq)
endmodule

module movY (
  input  down,
  input  up,
  input  reset,
  output [2:0] posExit
);

  wire comparator_1_gt, comparator_2_lt, nor_1_out;
  wire [1:0] and_2_out;
  wire [2:0] adder_1_out, multiplexer_1_out, multiplexer_2_out, subtractor_1_out;

  nor nor_1 (nor_1_out, down, up);
  Register #(.width(3)) register_1 (.D(multiplexer_2_out), .clk(nor_1_out), .Q(posExit));  // open: en, clr
  Comparator #(.mode("unsigned"), .width(3)) comparator_1 (
    .a(posExit), .b(3'b000), .gt(comparator_1_gt));  // open: eq, lt
  Comparator #(.mode("unsigned"), .width(3)) comparator_2 (
    .a(posExit), .b(3'b111), .lt(comparator_2_lt));  // open: gt, eq
  Adder #(.width(3)) adder_1 (.a(posExit), .b(3'b001), .out(adder_1_out));  // open: cin, cout
  Subtractor #(.width(3)) subtractor_1 (.a(posExit), .b(3'b001), .out(subtractor_1_out));  // open: bin, bout
  and and_1 (and_2_out[1], down, comparator_1_gt);
  and and_2 (and_2_out[0], up, comparator_2_lt);
  Multiplexer #(.select(2), .width(3)) multiplexer_1 (
    .in0(posExit), .in1(adder_1_out), .in2(subtractor_1_out), .in3(posExit), .out(multiplexer_1_out),
    .sel(and_2_out));
  Multiplexer #(.width(3)) multiplexer_2 (.in0(multiplexer_1_out), .in1(3'b000), .out(multiplexer_2_out), .sel(reset));

  // Notes on the sheet:
  //   x+1 (arriba)
  //    (01 ar)
  //   x-1 (abajo)
  //   codificador
  //   aca decide si puede moverse o no
  //   (10 ab)
endmodule

module contador (
  input  clock,
  input  reset,
  output bit9,
  output out_4,
  output out_5,
  output out_6,
  output out_7,
  output out_8,
  output out_9,
  output out_10,
  output out_11,
  output bit0,
  output [3:0] salDec,
  output [3:0] salCent,
  output [3:0] salUni
);

  wire and_1_out, and_2_out, comparator_1_eq, comparator_2_eq, comparator_3_eq, comparator_4_eq,
       comparator_5_eq, comparator_6_gt, or_1_out;
  wire [3:0] adder_2_out, adder_3_out, multiplexer_1_out, multiplexer_2_out, multiplexer_3_out;
  wire [9:0] adder_1_out, ram_1_dout;

  Register #(.width(4)) register_1 (.D(multiplexer_1_out), .clk(and_1_out), .Q(salCent), .clr(reset));  // open: en
  Multiplexer #(.select(4), .width(4)) multiplexer_1 (
    .in0(4'b0001), .in1(4'b0010), .in2(4'b0011), .in3(4'b0100), .in4(4'b0101), .in5(4'b0110), .in6(4'b0111),
    .in7(4'b1000), .in8(4'b1001), .in9(4'b0000), .out(multiplexer_1_out), .sel(salCent));  // open: in10, in11, in12, in13, in14, in15
  Comparator #(.mode("unsigned"), .width(10)) comparator_1 (
    .a({bit9, out_4, out_5, out_6, out_7, out_8, out_9, out_10, out_11, bit0}), .b(10'h3e8),
    .eq(comparator_1_eq));  // open: gt, lt
  Adder #(.width(10)) adder_1 (
    .a({bit9, out_4, out_5, out_6, out_7, out_8, out_9, out_10, out_11, bit0}), .b(10'h5), .out(adder_1_out));  // open: cin, cout
  Register #(.width(4)) register_2 (.D(multiplexer_2_out), .clk(and_2_out), .Q(salDec), .clr(reset));  // open: en
  Register #(.width(10)) register_3 (
    .D(adder_1_out), .clk(clock), .Q({bit9, out_4, out_5, out_6, out_7, out_8, out_9, out_10, out_11, bit0}),
    .clr(or_1_out));  // open: en
  or or_1 (or_1_out, comparator_1_eq, reset);
  and and_1 (and_1_out, comparator_3_eq, comparator_2_eq);
  Comparator #(.width(4)) comparator_2 (.a(4'b0000), .b(salDec), .eq(comparator_2_eq));  // open: gt, lt
  Adder #(.width(4)) adder_2 (.a(4'b0000), .b(salDec), .out(adder_2_out));  // open: cin, cout
  Multiplexer #(.select(4), .width(4)) multiplexer_2 (
    .in0(4'b0001), .in1(4'b0010), .in2(4'b0011), .in3(4'b0100), .in4(4'b0101), .in5(4'b0110), .in6(4'b0111),
    .in7(4'b1000), .in8(4'b1001), .in9(4'b0000), .out(multiplexer_2_out), .sel(salDec));  // open: in10, in11, in12, in13, in14, in15
  Comparator #(.width(4)) comparator_3 (.a(adder_2_out), .b(4'b0000), .eq(comparator_3_eq));  // open: gt, lt
  Register #(.width(4)) register_4 (.D(multiplexer_3_out), .clk(clock), .Q(salUni), .clr(reset));  // open: en
  RAM #(.addrWidth(2), .dataWidth(10)) ram_1 (
    .addr(2'b01), .we(comparator_6_gt), .clk(comparator_6_gt),
    .din({bit9, out_4, out_5, out_6, out_7, out_8, out_9, out_10, out_11, bit0}), .dout(ram_1_dout));  // open: oe
  Comparator #(.width(4)) comparator_4 (.a(4'b0000), .b(salUni), .eq(comparator_4_eq));  // open: gt, lt
  Adder #(.width(4)) adder_3 (.a(4'b0000), .b(salUni), .out(adder_3_out));  // open: cin, cout
  Multiplexer #(.select(4), .width(4)) multiplexer_3 (
    .in0(4'b0101), .in5(4'b0000), .out(multiplexer_3_out), .sel(salUni));  // open: in1, in2, in3, in4, in6, in7, in8, in9, in10, in11, in12, in13, in14, in15
  and and_2 (and_2_out, comparator_4_eq, comparator_5_eq);
  Comparator #(.width(4)) comparator_5 (.a(adder_3_out), .b(4'b0000), .eq(comparator_5_eq));  // open: gt, lt
  Comparator #(.width(10)) comparator_6 (
    .a({bit9, out_4, out_5, out_6, out_7, out_8, out_9, out_10, out_11, bit0}), .b(ram_1_dout),
    .gt(comparator_6_gt));  // open: eq, lt

  // Notes on the sheet:
  //   contador actual
  //   siguiente numero a mostrar
  //   en todos los mux, estos deciden cual es el 
endmodule
