// Logisim project mainAlDia.circ as structural Verilog: 3 circuits, main circuit main
module main (
);

  wire and_1_out, and_5_out, and_6_out, button_2_out, button_3_out, button_4_out, button_5_out, clock_1_out,
       clock_2_out, comparator_1_eq, comparator_2_eq, comparator_3_eq, comparator_4_eq, comparator_5_eq,
       comparator_6_eq, comparator_7_eq, comparator_8_eq, comparator_9_gt, d_ff_1_q, et1, et2, et3, et4, et5,
       et6, et7, et8, et9, et10, et11, et12, et13, et14, et15, et16, not_4_out, not_5_out, or_5_out,
       por_1_out, register_1_q, shift_register_1_p1, shift_register_2_p11, shift_register_3_p10;
  wire [2:0] counter_1_q, movy_1_posexit;
  wire [3:0] movx_1_posexit;
  wire [15:0] and_2_out, and_3_out, and_4_out, decoder_1_out15, multiplexer_1_out, multiplexer_2_out,
       multiplexer_3_out, multiplexer_4_out, multiplexer_5_out, multiplexer_6_out, multiplexer_7_out,
       multiplexer_8_out, multiplexer_9_out, multiplexer_10_out, multiplexer_11_out, or_1_out, or_2_out,
       or_3_out, or_4_out, shift_register_1_p12, shift_register_3_p33;

  Button button_1 ();  // open: out
  movX movx_1 (.left(button_2_out), .right(button_5_out), .posExit(movx_1_posexit));
  movY movy_1 (.down(button_4_out), .up(button_3_out), .posExit(movy_1_posexit));
  Decoder #(.select(4)) decoder_1 (
    .out0(decoder_1_out15[15]), .out1(decoder_1_out15[14]), .out2(decoder_1_out15[13]),
    .out3(decoder_1_out15[12]), .out4(decoder_1_out15[11]), .out5(decoder_1_out15[10]),
    .out6(decoder_1_out15[9]), .out7(decoder_1_out15[8]), .out8(decoder_1_out15[7]),
    .out9(decoder_1_out15[6]), .out10(decoder_1_out15[5]), .out11(decoder_1_out15[4]),
    .out12(decoder_1_out15[3]), .out13(decoder_1_out15[2]), .out14(decoder_1_out15[1]),
    .out15(decoder_1_out15[0]), .sel(movx_1_posexit));  // open: en
  Clock clock_1 (.out(clock_1_out));
  POR #(.porsize(1)) por_1 (.out(por_1_out));
  and and_1 (and_1_out, not_4_out, clock_1_out);
  // Shift_Register #(.length(16)) shift_register_1: pin names not known; wires that end beside it: shift_register_1_p1, and_1_out, shift_register_1_p12[15], 1'b1, 1'b0, 1'b0, 1'b0, 1'b1, 1'b1, 1'b0, por_1_out, shift_register_1_p12[0], shift_register_1_p12[1], shift_register_1_p12[2], shift_register_1_p12[3], shift_register_1_p12[4], shift_register_1_p12[5], shift_register_1_p12[6]
  not not_1 (shift_register_1_p1, por_1_out);
  // Shift_Register #(.length(16)) shift_register_2: pin names not known; wires that end beside it: 1'b1, 1'b0, 1'b1, 1'b0, 1'b0, 1'b0, 1'b1, 1'b0, 1'b1, por_1_out, shift_register_2_p11, and_1_out, et16, 1'b0, 1'b1, 1'b0, 1'b1, 1'b1, 1'b1, 1'b0, 1'b0, shift_register_1_p12[15], shift_register_1_p12[7], shift_register_1_p12[8], shift_register_1_p12[9], shift_register_1_p12[10], shift_register_1_p12[11], shift_register_1_p12[12], shift_register_1_p12[13], shift_register_1_p12[14], et1, et2, et3, et4, et5, et6, et7, et8
  not not_2 (shift_register_2_p11, por_1_out);
  // Shift_Register #(.length(16)) shift_register_3: pin names not known; wires that end beside it: 1'b0, 1'b0, 1'b0, 1'b1, 1'b0, 1'b1, 1'b0, 1'b0, por_1_out, shift_register_3_p10, and_1_out, shift_register_3_p33[15], 1'b0, 1'b1, 1'b0, 1'b1, 1'b0, 1'b0, 1'b0, 1'b1, 1'b1, 1'b0, 1'b0, 1'b0, et16, et9, et10, et11, et12, et13, et14, et15, shift_register_3_p33[0], shift_register_3_p33[1], shift_register_3_p33[2], shift_register_3_p33[3], shift_register_3_p33[4], shift_register_3_p33[5], shift_register_3_p33[6], shift_register_3_p33[7], shift_register_3_p33[8], shift_register_3_p33[9], shift_register_3_p33[10], shift_register_3_p33[11]
  not not_3 (shift_register_3_p10, por_1_out);
  Comparator #(.mode("unsigned"), .width(3)) comparator_1 (
    .a(movy_1_posexit), .b(3'b111), .eq(comparator_1_eq));  // open: gt, lt
  Comparator #(.mode("unsigned"), .width(3)) comparator_2 (
    .a(movy_1_posexit), .b(3'b110), .eq(comparator_2_eq));  // open: gt, lt
  Comparator #(.mode("unsigned"), .width(3)) comparator_3 (
    .a(movy_1_posexit), .b(3'b101), .eq(comparator_3_eq));  // open: gt, lt
  Comparator #(.mode("unsigned"), .width(3)) comparator_4 (
    .a(movy_1_posexit), .b(3'b100), .eq(comparator_4_eq));  // open: gt, lt
  Comparator #(.mode("unsigned"), .width(3)) comparator_5 (
    .a(movy_1_posexit), .b(3'b011), .eq(comparator_5_eq));  // open: gt, lt
  Comparator #(.mode("unsigned"), .width(3)) comparator_6 (
    .a(movy_1_posexit), .b(3'b010), .eq(comparator_6_eq));  // open: gt, lt
  Comparator #(.mode("unsigned"), .width(3)) comparator_7 (
    .a(movy_1_posexit), .b(3'b001), .eq(comparator_7_eq));  // open: gt, lt
  Comparator #(.mode("unsigned"), .width(3)) comparator_8 (
    .a(movy_1_posexit), .b(3'b000), .eq(comparator_8_eq));  // open: gt, lt
  Multiplexer #(.width(16)) multiplexer_1 (
    .in0({16{1'b0}}), .in1(decoder_1_out15), .out(multiplexer_1_out), .sel(comparator_1_eq));
  Multiplexer #(.width(16)) multiplexer_2 (
    .in0({16{1'b0}}), .in1(decoder_1_out15), .out(multiplexer_2_out), .sel(comparator_2_eq));
  Multiplexer #(.width(16)) multiplexer_3 (
    .in0({16{1'b0}}), .in1(decoder_1_out15), .out(multiplexer_3_out), .sel(comparator_3_eq));
  Multiplexer #(.width(16)) multiplexer_4 (
    .in0({16{1'b0}}), .in1(decoder_1_out15), .out(multiplexer_4_out), .sel(comparator_4_eq));
  Multiplexer #(.width(16)) multiplexer_5 (
    .in0({16{1'b0}}), .in1(decoder_1_out15), .out(multiplexer_5_out), .sel(comparator_5_eq));
  Multiplexer #(.width(16)) multiplexer_6 (
    .in0({16{1'b0}}), .in1(decoder_1_out15), .out(multiplexer_6_out), .sel(comparator_6_eq));
  Multiplexer #(.width(16)) multiplexer_7 (
    .in0({16{1'b0}}), .in1(decoder_1_out15), .out(multiplexer_7_out), .sel(comparator_7_eq));
  Multiplexer #(.width(16)) multiplexer_8 (
    .in0({16{1'b0}}), .in1(decoder_1_out15), .out(multiplexer_8_out), .sel(comparator_8_eq));
  Multiplexer #(.width(16)) multiplexer_9 (
    .in0(shift_register_1_p12), .in1({16{1'b0}}), .out(multiplexer_9_out), .sel(register_1_q));
  Multiplexer #(.width(16)) multiplexer_10 (
    .in0({et1, et2, et3, et4, et5, et6, et7, et8, et9, et10, et11, et12, et13, et14, et15, et16}),
    .in1({16{1'b0}}), .out(multiplexer_10_out), .sel(register_1_q));
  Multiplexer #(.width(16)) multiplexer_11 (
    .in0(shift_register_3_p33), .in1({16{1'b0}}), .out(multiplexer_11_out), .sel(register_1_q));
  assign or_1_out = multiplexer_2_out | multiplexer_9_out;  // OR_Gate or_1, 16 bits wide
  assign or_2_out = multiplexer_5_out | multiplexer_10_out;  // OR_Gate or_2, 16 bits wide
  assign or_3_out = multiplexer_7_out | multiplexer_11_out;  // OR_Gate or_3, 16 bits wide
  DotMatrix #(.inputtype("row"), .matrixcols(16), .matrixrows(8)) dotmatrix_1 (
    .row0(multiplexer_1_out), .row1(or_1_out), .row2(multiplexer_3_out), .row3(multiplexer_4_out),
    .row4(or_2_out), .row5(multiplexer_6_out), .row6(or_3_out), .row7(multiplexer_8_out));
  Button button_2 (.out(button_2_out));
  Button button_3 (.out(button_3_out));
  Button button_4 (.out(button_4_out));
  Button button_5 (.out(button_5_out));
  assign and_2_out = multiplexer_2_out & multiplexer_9_out;  // AND_Gate and_2, 16 bits wide
  assign and_3_out = multiplexer_10_out & multiplexer_5_out;  // AND_Gate and_3, 16 bits wide
  assign and_4_out = multiplexer_11_out & multiplexer_7_out;  // AND_Gate and_4, 16 bits wide
  assign or_4_out = and_2_out | and_3_out | and_4_out;  // OR_Gate or_4, 16 bits wide
  Comparator #(.mode("unsigned"), .width(16)) comparator_9 (
    .a(or_4_out), .b({16{1'b0}}), .gt(comparator_9_gt));  // open: eq, lt
  LED led_1 (.in(comparator_9_gt));
  Clock clock_2 (.out(clock_2_out));
  not not_4 (not_4_out, d_ff_1_q);
  D_Flip_Flop d_ff_1 (.D(or_5_out), .clk(clock_2_out), .Q(d_ff_1_q));  // open: Qn, preset, reset
  or or_5 (or_5_out, comparator_9_gt, d_ff_1_q);
  not not_5 (not_5_out, register_1_q);
  Register #(.width(1)) register_1 (.D(and_5_out), .clk(clock_2_out), .Q(register_1_q));  // open: en, clr
  and and_5 (and_5_out, not_5_out, d_ff_1_q);
  and and_6 (and_6_out, register_1_q, clock_2_out);
  Counter #(.max('h7), .width(3)) counter_1 (.clk(and_6_out), .Q(counter_1_q));  // open: clr, load, up, count, D, carry
  Comparator #(.width(3)) comparator_10 (.a(3'b110), .b(counter_1_q));  // open: gt, eq, lt

  // Notes on the sheet:
  //   Salida de posicionY
  //   Flag de Colisión
  //   Registro de Perder
  //   Cuenta 6 ticks dsp de perder, luego reinicio.
endmodule

module movX (
  input  left,
  input  right,
  output [3:0] posExit
);

  wire comparator_1_gt, comparator_2_lt, nor_1_out;
  wire [1:0] and_2_out;
  wire [3:0] adder_1_out, multiplexer_1_out, subtractor_1_out;

  Register #(.width(4)) register_1 (.D(multiplexer_1_out), .clk(nor_1_out), .Q(posExit));  // open: en, clr
  nor nor_1 (nor_1_out, left, right);
  Comparator #(.mode("unsigned"), .width(4)) comparator_1 (
    .a(posExit), .b(4'b0000), .gt(comparator_1_gt));  // open: eq, lt
  Comparator #(.mode("unsigned"), .width(4)) comparator_2 (
    .a(posExit), .b(4'b1111), .lt(comparator_2_lt));  // open: gt, eq
  Adder #(.width(4)) adder_1 (.a(posExit), .b(4'b0001), .out(adder_1_out));  // open: cin, cout
  Subtractor #(.width(4)) subtractor_1 (.a(posExit), .b(4'b0001), .out(subtractor_1_out));  // open: bin, bout
  and and_1 (and_2_out[1], left, comparator_1_gt);
  and and_2 (and_2_out[0], right, comparator_2_lt);
  Multiplexer #(.select(2), .width(4)) multiplexer_1 (
    .in0(posExit), .in1(adder_1_out), .in2(subtractor_1_out), .in3(posExit), .out(multiplexer_1_out),
    .sel(and_2_out));

  // Notes on the sheet:
  //   x+1 (der)
  //    (01 der)
  //   x-1 (izq)
  //   codificador
  //   aca decide si puede moverse o no
  //   (10 izq)
endmodule

module movY (
  input  down,
  input  up,
  output [2:0] posExit
);

  wire comparator_1_gt, comparator_2_lt, nor_1_out;
  wire [1:0] and_2_out;
  wire [2:0] adder_1_out, register_1_q, subtractor_1_out;

  nor nor_1 (nor_1_out, down, up);
  Register #(.width(3)) register_1 (.D(posExit), .clk(nor_1_out), .Q(register_1_q));  // open: en, clr
  Comparator #(.mode("unsigned"), .width(3)) comparator_1 (
    .a(register_1_q), .b(3'b000), .gt(comparator_1_gt));  // open: eq, lt
  Comparator #(.mode("unsigned"), .width(3)) comparator_2 (
    .a(register_1_q), .b(3'b111), .lt(comparator_2_lt));  // open: gt, eq
  Adder #(.width(3)) adder_1 (.a(register_1_q), .b(3'b001), .out(adder_1_out));  // open: cin, cout
  Subtractor #(.width(3)) subtractor_1 (.a(register_1_q), .b(3'b001), .out(subtractor_1_out));  // open: bin, bout
  and and_1 (and_2_out[1], down, comparator_1_gt);
  and and_2 (and_2_out[0], up, comparator_2_lt);
  Multiplexer #(.select(2), .width(3)) multiplexer_1 (
    .in0(register_1_q), .in1(adder_1_out), .in2(subtractor_1_out), .in3(register_1_q), .out(posExit),
    .sel(and_2_out));

  // Notes on the sheet:
  //   x+1 (arriba)
  //    (01 ar)
  //   x-1 (abajo)
  //   codificador
  //   aca decide si puede moverse o no
  //   (10 ab)
endmodule
