// Logisim project maquinaEstado.circ as structural Verilog: 1 circuit, main circuit ME
module ME (
  input  A,
  input  B,
  output PuertaA,
  output PuertaB
);

  wire and_1_out, and_2_out, and_3_out, and_4_out, CLK_out, not_1_out, not_2_out, not_3_out, not_4_out,
       not_5_out, not_6_out, not_7_out, or_1_out, or_2_out;

  not not_1 (not_1_out, A);
  not not_2 (not_2_out, PuertaA);
  not not_3 (not_3_out, PuertaB);
  not not_4 (not_4_out, PuertaA);
  not not_5 (not_5_out, PuertaB);
  not not_6 (not_6_out, PuertaA);
  not not_7 (not_7_out, B);
  and and_1 (and_1_out, PuertaA, not_1_out);
  and and_2 (and_2_out, A, not_2_out, not_3_out);
  and and_3 (and_3_out, not_4_out, not_5_out, B);
  and and_4 (and_4_out, not_6_out, PuertaB, not_7_out);
  or or_1 (or_1_out, and_1_out, and_2_out);
  or or_2 (or_2_out, and_3_out, and_4_out);
  D_Flip_Flop d_ff_1 (.D(or_1_out), .clk(CLK_out), .Q(PuertaA));  // open: Qn, preset, reset
  D_Flip_Flop d_ff_2 (.D(or_2_out), .clk(CLK_out), .Q(PuertaB));  // open: Qn, preset, reset
  Clock CLK (.out(CLK_out));

  // Notes on the sheet:
  //   Qb
  //   Qa
endmodule
