// Logisim project obligatorioComienzo - rama.circ as structural Verilog: 1 circuit, main circuit main
module main (
);

  wire clock_1_out, clock_2_out, clock_3_out, clock_4_out, clock_5_out, clock_6_out, comparator_1_eq,
       comparator_2_eq, comparator_3_eq, comparator_4_eq, comparator_5_eq, comparator_6_eq, comparator_7_eq,
       comparator_8_eq, et1, et2, et3, et4, et5, et6, et7, et8, et9, et10, et11, et12, et13, et14, et15,
       et16, por_1_out, por_2_out, shift_register_1_p1, shift_register_2_p10, shift_register_3_p11,
       shift_register_4_p1, shift_register_5_p11, shift_register_6_p10;
  wire [15:0] decoder_1_out0, multiplexer_1_out, multiplexer_2_out, multiplexer_3_out, multiplexer_4_out,
       multiplexer_5_out, multiplexer_6_out, multiplexer_7_out, multiplexer_8_out, or_1_out, or_2_out,
       or_3_out, shift_register_1_p13, shift_register_3_p35, shift_register_4_p12, shift_register_6_p33;

  POR #(.porsize(1)) por_1 (.out(por_1_out));
  Clock clock_1 (.out(clock_1_out));
  Clock clock_2 (.out(clock_2_out));
  Clock clock_3 (.out(clock_3_out));
  // Shift_Register #(.length(16)) shift_register_1: pin names not known; wires that end beside it: shift_register_1_p1, clock_1_out, shift_register_1_p13[15], 1'b1, 1'b0, 1'b0, 1'b0, 1'b1, 1'b1, 1'b0, 1'b1, por_1_out, shift_register_1_p13[0], shift_register_1_p13[1], shift_register_1_p13[2], shift_register_1_p13[3], shift_register_1_p13[4], shift_register_1_p13[5], shift_register_1_p13[6], shift_register_1_p13[7]
  not not_1 (shift_register_1_p1, por_1_out);
  // Shift_Register #(.length(16)) shift_register_2: pin names not known; wires that end beside it: 1'b0, 1'b1, 1'b0, 1'b0, 1'b0, 1'b1, 1'b0, 1'b1, por_1_out, shift_register_2_p10, clock_2_out, et16, 1'b0, 1'b1, 1'b0, 1'b1, 1'b1, 1'b1, 1'b0, shift_register_1_p13[15], shift_register_1_p13[8], shift_register_1_p13[9], shift_register_1_p13[10], shift_register_1_p13[11], shift_register_1_p13[12], shift_register_1_p13[13], shift_register_1_p13[14], et1, et2, et3, et4, et5, et6, et7
  not not_2 (shift_register_2_p10, por_1_out);
  // Shift_Register #(.length(16)) shift_register_3: pin names not known; wires that end beside it: 1'b0, 1'b0, 1'b0, 1'b0, 1'b1, 1'b0, 1'b1, 1'b0, 1'b0, por_1_out, shift_register_3_p11, clock_3_out, shift_register_3_p35[15], 1'b0, 1'b1, 1'b0, 1'b1, 1'b0, 1'b0, 1'b0, 1'b1, 1'b1, 1'b0, 1'b0, 1'b0, et16, et8, et9, et10, et11, et12, et13, et14, et15, shift_register_3_p35[0], shift_register_3_p35[1], shift_register_3_p35[2], shift_register_3_p35[3], shift_register_3_p35[4], shift_register_3_p35[5], shift_register_3_p35[6], shift_register_3_p35[7], shift_register_3_p35[8], shift_register_3_p35[9], shift_register_3_p35[10], shift_register_3_p35[11]
  not not_3 (shift_register_3_p11, por_1_out);
  DotMatrix #(.inputtype("row"), .matrixcols(16), .matrixrows(8)) dotmatrix_1 (
    .row1(shift_register_1_p13),
    .row4({et1, et2, et3, et4, et5, et6, et7, et8, et9, et10, et11, et12, et13, et14, et15, et16}),
    .row6(shift_register_3_p35), .row7(decoder_1_out0));  // open: row0, row2, row3, row5
  Button button_1 ();  // open: out
  Button button_2 ();  // open: out
  Button button_3 ();  // open: out
  Button button_4 ();  // open: out
  Decoder #(.select(4)) decoder_1 (
    .out0(decoder_1_out0[0]), .out1(decoder_1_out0[1]), .out2(decoder_1_out0[2]), .out3(decoder_1_out0[3]),
    .out4(decoder_1_out0[4]), .out5(decoder_1_out0[5]), .out6(decoder_1_out0[6]), .out7(decoder_1_out0[7]),
    .out8(decoder_1_out0[8]), .out9(decoder_1_out0[9]), .out10(decoder_1_out0[10]),
    .out11(decoder_1_out0[11]), .out12(decoder_1_out0[12]), .out13(decoder_1_out0[13]),
    .out14(decoder_1_out0[14]), .out15(decoder_1_out0[15]), .sel(4'b1001));  // open: en
  POR #(.porsize(1)) por_2 (.out(por_2_out));
  Clock clock_4 (.out(clock_4_out));
  Clock clock_5 (.out(clock_5_out));
  Clock clock_6 (.out(clock_6_out));
  // Shift_Register #(.length(16)) shift_register_4: pin names not known; wires that end beside it: shift_register_4_p1, clock_4_out, shift_register_4_p12[15], 1'b1, 1'b0, 1'b0, 1'b0, 1'b1, 1'b1, 1'b0, por_2_out, shift_register_4_p12[0], shift_register_4_p12[1], shift_register_4_p12[2], shift_register_4_p12[3], shift_register_4_p12[4], shift_register_4_p12[5], shift_register_4_p12[6]
  not not_4 (shift_register_4_p1, por_2_out);
  // Shift_Register #(.length(16)) shift_register_5: pin names not known; wires that end beside it: 1'b1, 1'b0, 1'b1, 1'b0, 1'b0, 1'b0, 1'b1, 1'b0, 1'b1, por_2_out, shift_register_5_p11, clock_5_out, et16, 1'b0, 1'b1, 1'b0, 1'b1, 1'b1, 1'b1, 1'b0, 1'b0, shift_register_4_p12[15], shift_register_4_p12[7], shift_register_4_p12[8], shift_register_4_p12[9], shift_register_4_p12[10], shift_register_4_p12[11], shift_register_4_p12[12], shift_register_4_p12[13], shift_register_4_p12[14], et1, et2, et3, et4, et5, et6, et7, et8
  not not_5 (shift_register_5_p11, por_2_out);
  // Shift_Register #(.length(16)) shift_register_6: pin names not known; wires that end beside it: 1'b0, 1'b0, 1'b0, 1'b1, 1'b0, 1'b1, 1'b0, 1'b0, por_2_out, shift_register_6_p10, clock_6_out, shift_register_6_p33[15], 1'b0, 1'b1, 1'b0, 1'b1, 1'b0, 1'b0, 1'b0, 1'b1, 1'b1, 1'b0, 1'b0, 1'b0, et16, et9, et10, et11, et12, et13, et14, et15, shift_register_6_p33[0], shift_register_6_p33[1], shift_register_6_p33[2], shift_register_6_p33[3], shift_register_6_p33[4], shift_register_6_p33[5], shift_register_6_p33[6], shift_register_6_p33[7], shift_register_6_p33[8], shift_register_6_p33[9], shift_register_6_p33[10], shift_register_6_p33[11]
  not not_6 (shift_register_6_p10, por_2_out);
  Comparator #(.mode("unsigned"), .width(3)) comparator_1 (
    .a(3'b111), .b(3'b000), .eq(comparator_1_eq));  // open: gt, lt
  Comparator #(.mode("unsigned"), .width(3)) comparator_2 (
    .a(3'b111), .b(3'b001), .eq(comparator_2_eq));  // open: gt, lt
  Comparator #(.mode("unsigned"), .width(3)) comparator_3 (
    .a(3'b111), .b(3'b010), .eq(comparator_3_eq));  // open: gt, lt
  Comparator #(.mode("unsigned"), .width(3)) comparator_4 (
    .a(3'b111), .b(3'b011), .eq(comparator_4_eq));  // open: gt, lt
  Comparator #(.mode("unsigned"), .width(3)) comparator_5 (
    .a(3'b111), .b(3'b100), .eq(comparator_5_eq));  // open: gt, lt
  Comparator #(.mode("unsigned"), .width(3)) comparator_6 (
    .a(3'b111), .b(3'b101), .eq(comparator_6_eq));  // open: gt, lt
  Comparator #(.mode("unsigned"), .width(3)) comparator_7 (
    .a(3'b111), .b(3'b110), .eq(comparator_7_eq));  // open: gt, lt
  Comparator #(.mode("unsigned"), .width(3)) comparator_8 (
    .a(3'b111), .b(3'b111), .eq(comparator_8_eq));  // open: gt, lt
  Multiplexer #(.width(16)) multiplexer_1 (
    .in0({16{1'b0}}), .in1(decoder_1_out0), .out(multiplexer_1_out), .sel(comparator_1_eq));
  Multiplexer #(.width(16)) multiplexer_2 (
    .in0({16{1'b0}}), .in1(decoder_1_out0), .out(multiplexer_2_out), .sel(comparator_2_eq));
  Multiplexer #(.width(16)) multiplexer_3 (
    .in0({16{1'b0}}), .in1(decoder_1_out0), .out(multiplexer_3_out), .sel(comparator_3_eq));
  Multiplexer #(.width(16)) multiplexer_4 (
    .in0({16{1'b0}}), .in1(decoder_1_out0), .out(multiplexer_4_out), .sel(comparator_4_eq));
  Multiplexer #(.width(16)) multiplexer_5 (
    .in0({16{1'b0}}), .in1(decoder_1_out0), .out(multiplexer_5_out), .sel(comparator_5_eq));
  Multiplexer #(.width(16)) multiplexer_6 (
    .in0({16{1'b0}}), .in1(decoder_1_out0), .out(multiplexer_6_out), .sel(comparator_6_eq));
  Multiplexer #(.width(16)) multiplexer_7 (
    .in0({16{1'b0}}), .in1(decoder_1_out0), .out(multiplexer_7_out), .sel(comparator_7_eq));
  Multiplexer #(.width(16)) multiplexer_8 (
    .in0({16{1'b0}}), .in1(decoder_1_out0), .out(multiplexer_8_out), .sel(comparator_8_eq));
  assign or_1_out = multiplexer_2_out | shift_register_4_p12;  // OR_Gate or_1, 16 bits wide
  assign or_2_out = multiplexer_5_out | {et1, et2, et3, et4, et5, et6, et7, et8, et9, et10, et11, et12, et13, et14, et15, et16};  // OR_Gate or_2, 16 bits wide
  assign or_3_out = multiplexer_7_out | shift_register_6_p33;  // OR_Gate or_3, 16 bits wide
  DotMatrix #(.inputtype("row"), .matrixcols(16), .matrixrows(8)) dotmatrix_2 (
    .row0(multiplexer_1_out), .row1(or_1_out), .row2(multiplexer_3_out), .row3(multiplexer_4_out),
    .row4(or_2_out), .row5(multiplexer_6_out), .row6(or_3_out), .row7(multiplexer_8_out));

  // Notes on the sheet:
  //   Entrada de la posicion(x) del jugador 4 bits
  //   bus de 16 bits con quince 0s y un 1
  //   tiene que entrar, segun la posicion Y elegida con comparadores
  //   Salida de posicionY
  //   DONDE CORRESPONDE VA UN OR CON EL SHIFT REGISTER D ELOS AUTOS
endmodule
