// Logisim project obligatorioComienzo.circ as structural Verilog: 1 circuit, main circuit main
module main (
);

  wire clock_1_out, clock_2_out, clock_3_out, et1, et2, et3, et4, et5, et6, et7, et8, et9, et10, et11, et12,
       et13, et14, et15, et16, por_1_out, shift_register_1_p1, shift_register_2_p10, shift_register_3_p11;
  wire [15:0] shift_register_1_p13, shift_register_3_p35, undriven;

  POR #(.porsize(1)) por_1 (.out(por_1_out));
  Clock clock_1 (.out(clock_1_out));
  Clock clock_2 (.out(clock_2_out));
  Clock clock_3 (.out(clock_3_out));
  // Shift_Register #(.length(16)) shift_register_1: pin names not known; wires that end beside it: shift_register_1_p1, clock_1_out, shift_register_1_p13[15], 1'b1, 1'b0, 1'b0, 1'b0, 1'b1, 1'b1, 1'b0, 1'b1, por_1_out, shift_register_1_p13[0], shift_register_1_p13[1], shift_register_1_p13[2], shift_register_1_p13[3], shift_register_1_p13[4], shift_register_1_p13[5], shift_register_1_p13[6], shift_register_1_p13[7]
  not not_1 (shift_register_1_p1, por_1_out);
  // Shift_Register #(.length(16)) shift_register_2: pin names not known; wires that end beside it: 1'b0, 1'b1, 1'b0, 1'b0, 1'b0, 1'b1, 1'b0, 1'b1, por_1_out, shift_register_2_p10, clock_2_out, et16, 1'b0, 1'b1, 1'b0, 1'b1, 1'b1, 1'b1, 1'b0, shift_register_1_p13[15], shift_register_1_p13[8], shift_register_1_p13[9], shift_register_1_p13[10], shift_register_1_p13[11], shift_register_1_p13[12], shift_register_1_p13[13], shift_register_1_p13[14], et1, et2, et3, et4, et5, et6, et7
  not not_2 (shift_register_2_p10, por_1_out);
  // Shift_Register #(.length(16)) shift_register_3: pin names not known; wires that end beside it: 1'b0, 1'b0, 1'b0, 1'b0, 1'b1, 1'b0, 1'b1, 1'b0, 1'b0, por_1_out, shift_register_3_p11, clock_3_out, shift_register_3_p35[15], 1'b0, 1'b1, 1'b0, 1'b1, 1'b0, 1'b0, 1'b0, 1'b1, 1'b1, 1'b0, 1'b0, 1'b0, et16, et8, et9, et10, et11, et12, et13, et14, et15, shift_register_3_p35[0], shift_register_3_p35[1], shift_register_3_p35[2], shift_register_3_p35[3], shift_register_3_p35[4], shift_register_3_p35[5], shift_register_3_p35[6], shift_register_3_p35[7], shift_register_3_p35[8], shift_register_3_p35[9], shift_register_3_p35[10], shift_register_3_p35[11]
  not not_3 (shift_register_3_p11, por_1_out);
  DotMatrix #(.inputtype("row"), .matrixcols(16), .matrixrows(8)) dotmatrix_1 (
    .row1(shift_register_1_p13),
    .row4({et1, et2, et3, et4, et5, et6, et7, et8, et9, et10, et11, et12, et13, et14, et15, et16}),
    .row6(shift_register_3_p35), .row7(undriven));  // open: row0, row2, row3, row5
  Button button_1 ();  // open: out
  Button button_2 ();  // open: out
  Button button_3 ();  // open: out
  Button button_4 ();  // open: out
endmodule
