// Logisim project obligatorioJugador.circ as structural Verilog: 2 circuits, main circuit main
module main (
);

  wire clock_1_out, clock_2_out, clock_3_out, et1, et2, et3, et4, et5, et6, et7, et8, et9, et10, et11, et12,
       et13, et14, et15, et16;
  wire [15:0] shift_register_1_p3, shift_register_3_p11;

  Clock clock_1 (.out(clock_1_out));
  Clock clock_2 (.out(clock_2_out));
  Clock clock_3 (.out(clock_3_out));
  // Shift_Register #(.length(16)) shift_register_1: pin names not known; wires that end beside it: clock_1_out, shift_register_1_p3[15], shift_register_1_p3[0], shift_register_1_p3[1], shift_register_1_p3[2], shift_register_1_p3[3], shift_register_1_p3[4], shift_register_1_p3[5], shift_register_1_p3[6], shift_register_1_p3[7]
  // Shift_Register #(.length(16)) shift_register_2: pin names not known; wires that end beside it: clock_2_out, et16, shift_register_1_p3[15], shift_register_1_p3[8], shift_register_1_p3[9], shift_register_1_p3[10], shift_register_1_p3[11], shift_register_1_p3[12], shift_register_1_p3[13], shift_register_1_p3[14], et1, et2, et3, et4, et5, et6, et7, et8
  // Shift_Register #(.length(16)) shift_register_3: pin names not known; wires that end beside it: clock_3_out, shift_register_3_p11[15], et16, et9, et10, et11, et12, et13, et14, et15, shift_register_3_p11[0], shift_register_3_p11[1], shift_register_3_p11[2], shift_register_3_p11[3], shift_register_3_p11[4], shift_register_3_p11[5], shift_register_3_p11[6], shift_register_3_p11[7], shift_register_3_p11[8], shift_register_3_p11[9], shift_register_3_p11[10], shift_register_3_p11[11]
  DotMatrix #(.inputtype("row"), .matrixcols(16), .matrixrows(8)) dotmatrix_1 (
    .row1(shift_register_1_p3),
    .row4({et1, et2, et3, et4, et5, et6, et7, et8, et9, et10, et11, et12, et13, et14, et15, et16}),
    .row6(shift_register_3_p11));  // open: row0, row2, row3, row5, row7
  Register register_1 ();  // open: D, en, clk, Q, clr
endmodule

module Jugador_XY (
  input  reset_pos,
  input  left,
  input  right,
  input  up,
  input  down,
  output [3:0] x_actual,
  output mov_x,
  output [2:0] y_actual,
  output mov_y
);

  wire clk_x_out, clk_y_out;

  or or_1 (mov_x, left, right);
  or or_2 (mov_y, up, down);
  Counter #(.max('hf), .ongoal("stay"), .width(4)) REG_X (
    .load(reset_pos), .D(4'b1000), .count(mov_x), .Q(x_actual), .up(right), .clk(clk_x_out));  // open: carry, clr
  Clock clk_x (.out(clk_x_out));
  Counter #(.max('h7), .ongoal("stay"), .width(3)) REG_Y (
    .load(reset_pos), .D(3'b111), .count(mov_y), .Q(y_actual), .up(down), .clk(clk_y_out));  // open: carry, clr
  Clock clk_y (.out(clk_y_out));

  // Notes on the sheet:
  //   Jugador_XY: posicion del jugador con limites 16x8
  //   reset_pos carga X=8, Y=7. Los contadores quedan quietos en los bordes.
endmodule
